// Logisim project 1BitAdder_To_MultiBitAdder.circ as structural Verilog: 2 circuits, main circuit main
module main (
  input  [1:0] in_1,
  input  [1:0] in_2,
  output [2:0] out_3
);

  wire n1bitadder_1_overflow, n1bitadder_1_this, n1bitadder_2_overflow, n1bitadder_2_this;
  wire [1:0] bit_extender_1_out;

  _1BitAdder u_1bitadder_1 (
    .OverflowInput(1'b0), .Num1(in_1[0]), .Num2(in_2[0]), .Overflow(n1bitadder_1_overflow),
    .This(n1bitadder_1_this));
  _1BitAdder u_1bitadder_2 (
    .OverflowInput(n1bitadder_1_overflow), .Num1(in_1[1]), .Num2(in_2[1]), .Overflow(n1bitadder_2_overflow),
    .This(n1bitadder_2_this));
  assign bit_extender_1_out = {{1{n1bitadder_2_this}}, n1bitadder_1_this};  // Bit_Extender bit_extender_1
  assign out_3 = {{1{n1bitadder_2_overflow}}, bit_extender_1_out};  // Bit_Extender bit_extender_2
endmodule

module _1BitAdder (
  input  OverflowInput,
  input  Num1,
  input  Num2,
  output This,
  output Overflow
);

  wire and_1_out, and_2_out, and_3_out;

  and and_1 (and_1_out, OverflowInput, Num1);
  and and_2 (and_2_out, OverflowInput, Num2);
  or or_1 (Overflow, and_1_out, and_2_out, and_3_out);
  and and_3 (and_3_out, Num1, Num2);
  xor xor_1 (This, OverflowInput, Num1, Num2);
endmodule
