// Logisim project 4BitArrangeCircuit.circ as structural Verilog: 3 circuits, main circuit 4bit_sort
module _4bit_sort (
  input  [3:0] A,
  input  [3:0] B,
  input  [3:0] C,
  input  [3:0] D,
  output [3:0] _1,
  output [3:0] _2,
  output [3:0] _3,
  output [3:0] _4
);

  wire comparator_1_eq, comparator_1_lt, comparator_2_eq, comparator_2_lt, comparator_3_eq, comparator_3_lt,
       comparator_4_eq, comparator_4_lt, comparator_5_eq, comparator_5_lt, not_1_out, not_2_out, not_3_out,
       not_4_out, not_5_out, or_1_out, or_2_out, or_3_out, or_4_out, or_5_out;
  wire [3:0] n4bit_swap_1_out_4, n4bit_swap_1_out_5, n4bit_swap_2_out_4, n4bit_swap_2_out_5,
       n4bit_swap_3_out_5, n4bit_swap_4_out_4;

  Comparator #(.width(4), .mode("unsigned")) comparator_1 (
    .a(A), .b(B), .eq(comparator_1_eq), .lt(comparator_1_lt));  // open: gt
  or or_1 (or_1_out, comparator_1_eq, comparator_1_lt);
  not not_1 (not_1_out, or_1_out);
  not not_2 (not_2_out, or_2_out);
  or or_2 (or_2_out, comparator_2_eq, comparator_2_lt);
  Comparator #(.width(4), .mode("unsigned")) comparator_2 (
    .a(C), .b(D), .eq(comparator_2_eq), .lt(comparator_2_lt));  // open: gt
  _4bit_swap u_4bit_swap_1 (
    .in_1(A), .in_2(B), .Switch(not_1_out), .out_4(n4bit_swap_1_out_4), .out_5(n4bit_swap_1_out_5));
  _4bit_swap u_4bit_swap_2 (
    .in_1(C), .in_2(D), .Switch(not_2_out), .out_4(n4bit_swap_2_out_4), .out_5(n4bit_swap_2_out_5));
  Comparator #(.width(4), .mode("unsigned")) comparator_3 (
    .a(n4bit_swap_1_out_4), .b(n4bit_swap_2_out_4), .eq(comparator_3_eq), .lt(comparator_3_lt));  // open: gt
  Comparator #(.width(4), .mode("unsigned")) comparator_4 (
    .a(n4bit_swap_1_out_5), .b(n4bit_swap_2_out_5), .eq(comparator_4_eq), .lt(comparator_4_lt));  // open: gt
  not not_3 (not_3_out, or_3_out);
  or or_3 (or_3_out, comparator_3_eq, comparator_3_lt);
  _4bit_swap u_4bit_swap_3 (
    .in_1(n4bit_swap_1_out_4), .in_2(n4bit_swap_2_out_4), .Switch(not_3_out), .out_4(_1),
    .out_5(n4bit_swap_3_out_5));
  or or_4 (or_4_out, comparator_4_eq, comparator_4_lt);
  not not_4 (not_4_out, or_4_out);
  _4bit_swap u_4bit_swap_4 (
    .in_1(n4bit_swap_1_out_5), .in_2(n4bit_swap_2_out_5), .Switch(not_4_out), .out_4(n4bit_swap_4_out_4),
    .out_5(_4));
  or or_5 (or_5_out, comparator_5_eq, comparator_5_lt);
  not not_5 (not_5_out, or_5_out);
  Comparator #(.width(4), .mode("unsigned")) comparator_5 (
    .a(n4bit_swap_3_out_5), .b(n4bit_swap_4_out_4), .eq(comparator_5_eq), .lt(comparator_5_lt));  // open: gt
  _4bit_swap u_4bit_swap_5 (
    .in_1(n4bit_swap_3_out_5), .in_2(n4bit_swap_4_out_4), .Switch(not_5_out), .out_4(_2), .out_5(_3));
endmodule

module _1bit_swap (
  input  Input1,
  input  Input2,
  input  Switch,
  output Output1,
  output Output2
);

  wire and_1_out, and_2_out, and_3_out, and_4_out, not_1_out;

  not not_1 (not_1_out, Switch);
  and and_1 (and_1_out, Input1, not_1_out);
  and and_2 (and_2_out, Input2, Switch);
  and and_3 (and_3_out, Input2, not_1_out);
  and and_4 (and_4_out, Input1, Switch);
  or or_1 (Output1, and_1_out, and_2_out);
  or or_2 (Output2, and_3_out, and_4_out);
endmodule

module _4bit_swap (
  input  [3:0] in_1,
  input  [3:0] in_2,
  input  Switch,
  output [3:0] out_4,
  output [3:0] out_5
);

  wire n1bit_swap_1_output1, n1bit_swap_1_output2, n1bit_swap_2_output1, n1bit_swap_2_output2,
       n1bit_swap_3_output1, n1bit_swap_3_output2, n1bit_swap_4_output1, n1bit_swap_4_output2;
  wire [1:0] bit_extender_1_out, bit_extender_4_out;
  wire [2:0] bit_extender_2_out, bit_extender_3_out;

  _1bit_swap u_1bit_swap_1 (
    .Input1(in_1[0]), .Input2(in_2[0]), .Switch(Switch), .Output1(n1bit_swap_1_output1),
    .Output2(n1bit_swap_1_output2));
  _1bit_swap u_1bit_swap_2 (
    .Input1(in_1[1]), .Input2(in_2[1]), .Switch(Switch), .Output1(n1bit_swap_2_output1),
    .Output2(n1bit_swap_2_output2));
  _1bit_swap u_1bit_swap_3 (
    .Input1(in_1[2]), .Input2(in_2[2]), .Switch(Switch), .Output1(n1bit_swap_3_output1),
    .Output2(n1bit_swap_3_output2));
  _1bit_swap u_1bit_swap_4 (
    .Input1(in_1[3]), .Input2(in_2[3]), .Switch(Switch), .Output1(n1bit_swap_4_output1),
    .Output2(n1bit_swap_4_output2));
  assign bit_extender_1_out = {{1{n1bit_swap_2_output2}}, n1bit_swap_1_output2};  // Bit_Extender bit_extender_1
  assign bit_extender_2_out = {{1{n1bit_swap_3_output2}}, bit_extender_1_out};  // Bit_Extender bit_extender_2
  assign bit_extender_3_out = {{1{n1bit_swap_3_output1}}, bit_extender_4_out};  // Bit_Extender bit_extender_3
  assign bit_extender_4_out = {{1{n1bit_swap_2_output1}}, n1bit_swap_1_output1};  // Bit_Extender bit_extender_4
  assign out_5 = {{1{n1bit_swap_4_output2}}, bit_extender_2_out};  // Bit_Extender bit_extender_5
  assign out_4 = {{1{n1bit_swap_4_output1}}, bit_extender_3_out};  // Bit_Extender bit_extender_6

  // Other names for the same wires on the sheet: Ctrl = Switch
endmodule
