// Logisim project 4bit_arrange_2.circ as structural Verilog: 1 circuit, main circuit 4bit_arrange_2
module _4bit_arrange_2 (
  input  [3:0] in_1,
  input  [3:0] in_2,
  output [3:0] out_3,
  output [3:0] out_4
);

  wire comparator_1_eq, comparator_1_gt, comparator_1_lt, not_1_out, not_2_out, or_1_out;

  Comparator #(.width(4), .mode("unsigned")) comparator_1 (
    .a(in_1), .b(in_2), .gt(comparator_1_gt), .eq(comparator_1_eq), .lt(comparator_1_lt));
  Multiplexer #(.width(4), .enable("false")) multiplexer_1 (.in0(in_1), .in1(in_2), .out(out_3), .sel(not_1_out));
  not not_1 (not_1_out, or_1_out);
  not not_2 (not_2_out, comparator_1_lt);
  or or_1 (or_1_out, comparator_1_gt, comparator_1_eq);
  Multiplexer #(.width(4), .enable("false")) multiplexer_2 (.in0(in_1), .in1(in_2), .out(out_4), .sel(not_2_out));
endmodule
