// Logisim project FullAdder.circ as structural Verilog: 1 circuit, main circuit main
module main (
  input  a,
  input  b,
  input  c,
  output F1,
  output F2
);

  wire and_1_out, and_2_out, and_3_out, and_4_out, or_1_out, or_2_out;

  and and_1 (and_1_out, a, b);
  or or_1 (or_1_out, b, a);
  and and_2 (and_2_out, or_1_out, c);
  or or_2 (or_2_out, or_1_out, c);
  and and_3 (and_3_out, c, and_1_out);
  or or_3 (F1, and_1_out, and_2_out);
  and and_4 (and_4_out, ~F1, or_2_out);  // AND_Gate
  or or_4 (F2, and_4_out, and_3_out);
endmodule
