// Logisim project MatrixFastPower4Fibonacci.circ as structural Verilog: 4 circuits, main circuit Matrix^2
module circulation (
  input  [31:0] in_1,
  output [31:0] out_2
);

  wire bitselector_1_out, clock_1_out, comparator_1_eq, comparator_1_gt, fuck, muxe, or_2_out, r;
  wire [7:0] counter_2_q, counter_3_q;
  wire [31:0] and_1_out, controlled_buffer_1_out, controlled_buffer_2_out, controlled_buffer_3_out,
       controlled_buffer_4_out, controlled_buffer_5_out, controlled_buffer_6_out, controlled_buffer_7_out,
       controlled_buffer_8_out, counter_1_q, matmult_1_out_9, matmult_1_out_10, matmult_1_out_11,
       matmult_1_out_12, matrix_2_1_b1, matrix_2_1_b2, matrix_2_1_b3, matrix_2_1_b4, multiplexer_1_out,
       multiplexer_2_out, multiplexer_3_out, multiplexer_4_out, multiplexer_5_out, multiplexer_6_out,
       multiplexer_7_out, multiplexer_8_out, multiplexer_9_out, register_1_q, register_2_q, register_3_q,
       register_4_q, register_5_q, register_7_q, register_8_q, register_9_q, register_10_q, shifter_1_out,
       subtractor_1_out;

  Counter #(.width(32), .max('hffffffff)) counter_1 (
    .Q(counter_1_q), .clk(clock_1_out));  // open: load, D, count, carry, clr
  or or_1 (muxe, subtractor_1_out[0], subtractor_1_out[1], subtractor_1_out[2], subtractor_1_out[3], subtractor_1_out[4], subtractor_1_out[5], subtractor_1_out[6], subtractor_1_out[7], subtractor_1_out[8], subtractor_1_out[9], subtractor_1_out[10], subtractor_1_out[11], subtractor_1_out[12], subtractor_1_out[13], subtractor_1_out[14], subtractor_1_out[15], subtractor_1_out[17], subtractor_1_out[18], subtractor_1_out[19], subtractor_1_out[20], subtractor_1_out[21], subtractor_1_out[22], subtractor_1_out[23], subtractor_1_out[24], subtractor_1_out[25], subtractor_1_out[26], subtractor_1_out[27], subtractor_1_out[28], subtractor_1_out[29], subtractor_1_out[30], subtractor_1_out[31], subtractor_1_out[16]);
  Subtractor #(.width(32)) subtractor_1 (.a(counter_1_q), .b(32'h1), .out(subtractor_1_out));  // open: bin, bout
  Multiplexer #(.width(32), .enable("false")) multiplexer_1 (
    .in0(32'h1), .in1(matrix_2_1_b1), .out(multiplexer_1_out), .sel(muxe));
  Register #(.width(32)) register_1 (.D(multiplexer_1_out), .Q(register_1_q), .clk(clock_1_out), .clr(r));  // open: en
  Register #(.width(32)) register_2 (.D(multiplexer_2_out), .Q(register_2_q), .clk(clock_1_out), .clr(r));  // open: en
  Multiplexer #(.width(32), .enable("false")) multiplexer_2 (
    .in0(32'h1), .in1(matrix_2_1_b2), .out(multiplexer_2_out), .sel(muxe));
  Register #(.width(32)) register_3 (.D(multiplexer_3_out), .Q(register_3_q), .clk(clock_1_out), .clr(r));  // open: en
  Multiplexer #(.width(32), .enable("false")) multiplexer_3 (
    .in0(32'h1), .in1(matrix_2_1_b3), .out(multiplexer_3_out), .sel(muxe));
  Multiplexer #(.width(32), .enable("false")) multiplexer_4 (
    .in0({32{1'b0}}), .in1(matrix_2_1_b4), .out(multiplexer_4_out), .sel(muxe));
  Register #(.width(32)) register_4 (.D(multiplexer_4_out), .Q(register_4_q), .clk(clock_1_out), .clr(r));  // open: en
  Multiplexer #(.width(32), .enable("false")) multiplexer_5 (
    .in0(in_1), .in1(shifter_1_out), .out(multiplexer_5_out), .sel(muxe));
  Register #(.width(32)) register_5 (.D(multiplexer_5_out), .Q(register_5_q), .clk(clock_1_out));  // open: en, clr
  Matrix_2 matrix_2_1 (
    .a1(register_1_q), .a2(register_2_q), .a3(register_3_q), .a4(register_4_q), .b1(matrix_2_1_b1),
    .b2(matrix_2_1_b2), .b3(matrix_2_1_b3), .b4(matrix_2_1_b4));
  Shifter #(.width(32), .shift("lr")) shifter_1 (.in(register_5_q), .\dist (5'b00001), .out(shifter_1_out));
  assign and_1_out = 32'h1 & multiplexer_5_out;  // AND_Gate and_1, 32 bits wide
  Clock clock_1 (.out(clock_1_out));
  BitSelector #(.width(32)) bitselector_1 (.in(and_1_out), .out(bitselector_1_out), .sel({5{1'b0}}));
  Multiplexer #(.width(32), .enable("false")) multiplexer_6 (
    .in0(32'h1), .in1(register_7_q), .out(multiplexer_6_out), .sel(fuck));
  Multiplexer #(.width(32), .enable("false")) multiplexer_7 (
    .in0({32{1'b0}}), .in1(register_8_q), .out(multiplexer_7_out), .sel(fuck));
  Multiplexer #(.width(32), .enable("false")) multiplexer_8 (
    .in0({32{1'b0}}), .in1(register_9_q), .out(multiplexer_8_out), .sel(fuck));
  Multiplexer #(.width(32), .enable("false")) multiplexer_9 (
    .in0(32'h1), .in1(register_10_q), .out(multiplexer_9_out), .sel(fuck));
  // Probe on and_1_out
  assign controlled_buffer_1_out = bitselector_1_out ? multiplexer_6_out : 32'bz;  // Controlled_Buffer controlled_buffer_1
  assign controlled_buffer_2_out = bitselector_1_out ? multiplexer_7_out : 32'bz;  // Controlled_Buffer controlled_buffer_2
  matmult matmult_1 (
    .a1(controlled_buffer_1_out), .a2(controlled_buffer_2_out), .a3(controlled_buffer_3_out),
    .a4(controlled_buffer_4_out), .b1(controlled_buffer_5_out), .b2(controlled_buffer_6_out),
    .b3(controlled_buffer_7_out), .b4(controlled_buffer_8_out), .out_9(matmult_1_out_9),
    .out_10(matmult_1_out_10), .out_11(matmult_1_out_11), .out_12(matmult_1_out_12));
  assign controlled_buffer_3_out = bitselector_1_out ? multiplexer_8_out : 32'bz;  // Controlled_Buffer controlled_buffer_3
  assign controlled_buffer_4_out = bitselector_1_out ? multiplexer_9_out : 32'bz;  // Controlled_Buffer controlled_buffer_4
  assign controlled_buffer_5_out = bitselector_1_out ? multiplexer_1_out : 32'bz;  // Controlled_Buffer controlled_buffer_5
  assign controlled_buffer_6_out = bitselector_1_out ? multiplexer_2_out : 32'bz;  // Controlled_Buffer controlled_buffer_6
  assign controlled_buffer_7_out = bitselector_1_out ? multiplexer_3_out : 32'bz;  // Controlled_Buffer controlled_buffer_7
  assign controlled_buffer_8_out = bitselector_1_out ? multiplexer_4_out : 32'bz;  // Controlled_Buffer controlled_buffer_8
  Register #(.width(32)) register_6 (.D(matmult_1_out_11), .Q(out_2), .clk(clock_1_out));  // open: en, clr
  Counter counter_2 (
    .Q({{4{counter_2_q[7]}}, counter_2_q[3:0]}), .clk(bitselector_1_out));  // open: load, D, count, carry, clr
  Register #(.width(32)) register_7 (.D(matmult_1_out_9), .Q(register_7_q), .clk(clock_1_out));  // open: en, clr
  Register #(.width(32)) register_8 (.D(matmult_1_out_10), .Q(register_8_q), .clk(clock_1_out));  // open: en, clr
  Register #(.width(32)) register_9 (.D(matmult_1_out_11), .Q(register_9_q), .clk(clock_1_out));  // open: en, clr
  Register #(.width(32)) register_10 (.D(matmult_1_out_12), .Q(register_10_q), .clk(clock_1_out));  // open: en, clr
  or or_2 (or_2_out, counter_2_q[0], counter_2_q[1], counter_2_q[2], counter_2_q[3], counter_2_q[7], counter_2_q[7], counter_2_q[7], counter_2_q[7]);
  Counter counter_3 (.count(or_2_out), .Q(counter_3_q), .clk(clock_1_out));  // open: load, D, carry, clr
  or or_3 (fuck, comparator_1_gt, comparator_1_eq);
  Comparator #(.mode("unsigned")) comparator_1 (
    .a(counter_3_q), .b(8'h1), .gt(comparator_1_gt), .eq(comparator_1_eq));  // open: lt
endmodule

module Matrix_2 (
  input  [31:0] a1,
  input  [31:0] a2,
  input  [31:0] a3,
  input  [31:0] a4,
  output [31:0] b1,
  output [31:0] b2,
  output [31:0] b3,
  output [31:0] b4
);

  wire [31:0] multiplier_1_out, multiplier_2_out, multiplier_3_out, multiplier_4_out, multiplier_5_out,
       multiplier_6_out, multiplier_7_out;

  Multiplier #(.width(32)) multiplier_1 (.a(a1), .b(a1), .out(multiplier_1_out));  // open: cin, cout
  Multiplier #(.width(32)) multiplier_2 (.a(a1), .b(a2), .out(multiplier_2_out));  // open: cin, cout
  Multiplier #(.width(32)) multiplier_3 (.a(a2), .b(a3), .out(multiplier_3_out));  // open: cin, cout
  Multiplier #(.width(32)) multiplier_4 (.a(a1), .b(a3), .out(multiplier_4_out));  // open: cin, cout
  Multiplier #(.width(32)) multiplier_5 (.a(a3), .b(a4), .out(multiplier_5_out));  // open: cin, cout
  Multiplier #(.width(32)) multiplier_6 (.a(a2), .b(a4), .out(multiplier_6_out));  // open: cin, cout
  Multiplier #(.width(32)) multiplier_7 (.a(a4), .b(a4), .out(multiplier_7_out));  // open: cin, cout
  Adder #(.width(32)) adder_1 (.a(multiplier_1_out), .b(multiplier_3_out), .out(b1));  // open: cin, cout
  Adder #(.width(32)) adder_2 (.a(multiplier_2_out), .b(multiplier_6_out), .out(b2));  // open: cin, cout
  Adder #(.width(32)) adder_3 (.a(multiplier_4_out), .b(multiplier_5_out), .out(b3));  // open: cin, cout
  Adder #(.width(32)) adder_4 (.a(multiplier_3_out), .b(multiplier_7_out), .out(b4));  // open: cin, cout
endmodule

module matmult (
  input  [31:0] a1,
  input  [31:0] a2,
  input  [31:0] a3,
  input  [31:0] a4,
  input  [31:0] b1,
  input  [31:0] b2,
  input  [31:0] b3,
  input  [31:0] b4,
  output [31:0] out_9,
  output [31:0] out_10,
  output [31:0] out_11,
  output [31:0] out_12
);

  wire [31:0] multiplier_1_out, multiplier_2_out, multiplier_3_out, multiplier_4_out, multiplier_5_out,
       multiplier_6_out, multiplier_7_out, multiplier_8_out;

  Multiplier #(.width(32)) multiplier_1 (.a(a1), .b(b1), .out(multiplier_1_out));  // open: cin, cout
  Multiplier #(.width(32)) multiplier_2 (.a(a1), .b(b2), .out(multiplier_2_out));  // open: cin, cout
  Multiplier #(.width(32)) multiplier_3 (.a(a2), .b(b3), .out(multiplier_3_out));  // open: cin, cout
  Multiplier #(.width(32)) multiplier_4 (.a(a2), .b(b4), .out(multiplier_4_out));  // open: cin, cout
  Multiplier #(.width(32)) multiplier_5 (.a(a3), .b(b1), .out(multiplier_5_out));  // open: cin, cout
  Multiplier #(.width(32)) multiplier_6 (.a(a3), .b(b2), .out(multiplier_6_out));  // open: cin, cout
  Multiplier #(.width(32)) multiplier_7 (.a(a4), .b(b3), .out(multiplier_7_out));  // open: cin, cout
  Multiplier #(.width(32)) multiplier_8 (.a(a4), .b(b4), .out(multiplier_8_out));  // open: cin, cout
  Adder #(.width(32)) adder_1 (.a(multiplier_1_out), .b(multiplier_3_out), .out(out_9));  // open: cin, cout
  Adder #(.width(32)) adder_2 (.a(multiplier_2_out), .b(multiplier_4_out), .out(out_10));  // open: cin, cout
  Adder #(.width(32)) adder_3 (.a(multiplier_5_out), .b(multiplier_7_out), .out(out_11));  // open: cin, cout
  Adder #(.width(32)) adder_4 (.a(multiplier_6_out), .b(multiplier_8_out), .out(out_12));  // open: cin, cout
endmodule

module main (
  input  [31:0] in_1,
  output [31:0] out_2
);

  circulation circulation_1 (.in_1(in_1), .out_2(out_2));
endmodule
