// Logisim project [p0.L0.Q1]crc.circ as structural Verilog: 4 circuits, main circuit CRC
module CRC (
  input  [7:0] A,
  input  [3:0] B,
  output [10:0] C
);

  _8_3bit_2div_4bit u_8_3bit_2div_4bit_1 (.A(A), .B(B), .out_3(C));
endmodule

module _4bit__2div (
  input  [3:0] DIVed_A,
  input  [3:0] DIV_B,
  output [3:0] Remainder
);

  wire [3:0] bit_extender_1_out, multiplier_1_out;

  assign bit_extender_1_out = {{3{1'b0}}, DIVed_A[3]};  // Bit_Extender bit_extender_1
  Multiplier #(.width(4)) multiplier_1 (.a(bit_extender_1_out), .b(DIV_B), .out(multiplier_1_out));  // open: cin, cout
  // Probe on multiplier_1_out
  assign Remainder = DIVed_A ^ multiplier_1_out;  // XOR_Gate xor_1, 4 bits wide

  // Notes on the sheet:
  //   A%2divB = A^(A[3] * B)
endmodule

module _8_3bit_2div_4bit (
  input  [7:0] A,
  input  [3:0] B,
  output [10:0] out_3
);

  wire [3:0] adder_1_out, adder_2_out, adder_3_out, adder_4_out, bit_extender_1_out, bit_extender_2_out,
       bit_extender_3_out, bit_extender_4_out, n4bit__2div_1_remainder, n4bit__2div_2_remainder,
       n4bit__2div_3_remainder, n4bit__2div_4_remainder, n4bit__2div_5_remainder, repeatcalc_1_out_4,
       repeatcalc_2_out_4, repeatcalc_3_out_4, shifter_1_out, shifter_2_out, shifter_4_out, shifter_5_out,
       shifter_6_out;
  wire [10:0] bit_extender_5_out, bit_extender_6_out, shifter_3_out;

  // Probe on A[7:4]
  _4bit__2div u_4bit__2div_1 (.DIVed_A(A[7:4]), .DIV_B(B), .Remainder(n4bit__2div_1_remainder));
  assign bit_extender_1_out = {{3{1'b0}}, A[0]};  // Bit_Extender bit_extender_1
  assign bit_extender_2_out = {{3{1'b0}}, A[1]};  // Bit_Extender bit_extender_2
  assign bit_extender_3_out = {{3{1'b0}}, A[2]};  // Bit_Extender bit_extender_3
  assign bit_extender_4_out = {{3{1'b0}}, A[3]};  // Bit_Extender bit_extender_4
  Shifter #(.width(4)) shifter_1 (.in(n4bit__2div_1_remainder), .\dist (2'b01), .out(shifter_1_out));
  // Probe on shifter_1_out
  Adder #(.width(4)) adder_1 (.a(bit_extender_4_out), .b(shifter_1_out), .out(adder_1_out));  // open: cin, cout
  // Probe on adder_1_out
  assign bit_extender_5_out = {{3{1'b0}}, A};  // Bit_Extender bit_extender_5
  _4bit__2div u_4bit__2div_2 (.DIVed_A(adder_1_out), .DIV_B(B), .Remainder(n4bit__2div_2_remainder));
  Shifter #(.width(4)) shifter_2 (.in(n4bit__2div_2_remainder), .\dist (2'b01), .out(shifter_2_out));
  Adder #(.width(4)) adder_2 (.a(bit_extender_3_out), .b(shifter_2_out), .out(adder_2_out));  // open: cin, cout
  // Probe on adder_2_out
  Shifter #(.width(11)) shifter_3 (.in(bit_extender_5_out), .\dist (4'b0011), .out(shifter_3_out));
  _4bit__2div u_4bit__2div_3 (.DIVed_A(adder_2_out), .DIV_B(B), .Remainder(n4bit__2div_3_remainder));
  Shifter #(.width(4)) shifter_4 (.in(n4bit__2div_3_remainder), .\dist (2'b01), .out(shifter_4_out));
  _4bit__2div u_4bit__2div_4 (.DIVed_A(adder_3_out), .DIV_B(B), .Remainder(n4bit__2div_4_remainder));
  Adder #(.width(4)) adder_3 (.a(bit_extender_2_out), .b(shifter_4_out), .out(adder_3_out));  // open: cin, cout
  // Probe on adder_3_out
  Shifter #(.width(4)) shifter_5 (.in(n4bit__2div_4_remainder), .\dist (2'b01), .out(shifter_5_out));
  Adder #(.width(4)) adder_4 (.a(bit_extender_1_out), .b(shifter_5_out), .out(adder_4_out));  // open: cin, cout
  // Probe on adder_4_out
  _4bit__2div u_4bit__2div_5 (.DIVed_A(adder_4_out), .DIV_B(B), .Remainder(n4bit__2div_5_remainder));
  Shifter #(.width(4)) shifter_6 (.in(n4bit__2div_5_remainder), .\dist (2'b01), .out(shifter_6_out));
  // Probe on shifter_6_out
  RepeatCalc repeatcalc_1 (.NextBit(1'b0), .LastRemainder(repeatcalc_2_out_4), .DIV_B(B), .out_4(repeatcalc_1_out_4));
  RepeatCalc repeatcalc_2 (.NextBit(1'b0), .LastRemainder(shifter_6_out), .DIV_B(B), .out_4(repeatcalc_2_out_4));
  // Probe on repeatcalc_2_out_4
  // Probe on repeatcalc_3_out_4[2:0]
  RepeatCalc repeatcalc_3 (.NextBit(1'b0), .LastRemainder(repeatcalc_1_out_4), .DIV_B(B), .out_4(repeatcalc_3_out_4));
  // Probe on repeatcalc_1_out_4
  assign bit_extender_6_out = {{8{1'b0}}, repeatcalc_3_out_4[2:0]};  // Bit_Extender bit_extender_6
  Adder #(.width(11)) adder_5 (.a(shifter_3_out), .b(bit_extender_6_out), .out(out_3));  // open: cin, cout

  // Notes on the sheet:
  //   A%2divB = A^(A[7] * B)
endmodule

module RepeatCalc (
  input  NextBit,
  input  [3:0] LastRemainder,
  input  [3:0] DIV_B,
  output [3:0] out_4
);

  wire [3:0] bit_extender_1_out, n4bit__2div_1_remainder, shifter_1_out;

  assign bit_extender_1_out = {{3{1'b0}}, NextBit};  // Bit_Extender bit_extender_1
  _4bit__2div u_4bit__2div_1 (.DIVed_A(LastRemainder), .DIV_B(DIV_B), .Remainder(n4bit__2div_1_remainder));
  Shifter #(.width(4)) shifter_1 (.in(n4bit__2div_1_remainder), .\dist (2'b01), .out(shifter_1_out));
  Adder #(.width(4)) adder_1 (.a(bit_extender_1_out), .b(shifter_1_out), .out(out_4));  // open: cin, cout
  // Probe on out_4
endmodule
