// Logisim project [p0.L0.Q3]ZhengZeExpression.circ as structural Verilog: 4 circuits, main circuit fsm
module fsm (
  input  [1:0] In,
  input  CLR,
  output Z
);

  wire and_1_out, CLK_out, outputlogic_1_value, register_2_q;
  wire [1:0] register_1_q, statechange_1_next0;

  StateChange statechange_1 (
    .In1(In[1]), .In0(In[0]), .Pre1(register_1_q[1]), .Pre0(register_1_q[0]), .Next1(statechange_1_next0[1]),
    .Next0(statechange_1_next0[0]));
  // Probe on statechange_1_next0
  Clock CLK (.out(CLK_out));
  Register #(.width(2)) register_1 (
    .D(statechange_1_next0), .Q(register_1_q), .clk(CLK_out), .clr(and_1_out));  // open: en
  Register #(.width(1)) register_2 (.D(CLR), .Q(register_2_q), .clk(CLK_out));  // open: en, clr
  // Probe on register_1_q
  and and_1 (and_1_out, register_2_q, CLR);
  // Probe on and_1_out
  OutputLogic outputlogic_1 (
    .State1(register_1_q[1]), .State0(register_1_q[0]), .In1(In[1]), .In0(In[0]), .Value(outputlogic_1_value));
  Multiplexer #(.enable("false")) multiplexer_1 (.in0(outputlogic_1_value), .in1(1'b0), .out(Z), .sel(and_1_out));
endmodule

module StateChange (
  input  In1,
  input  In0,
  input  Pre1,
  input  Pre0,
  output Next1,
  output Next0
);

  wire and_1_out, and_2_out, and_3_out, and_4_out, and_5_out, and_6_out, not_1_out, not_2_out, not_3_out,
       not_4_out, not_5_out, not_6_out, not_7_out, not_8_out, not_9_out, not_10_out, not_11_out;

  not not_1 (not_1_out, Pre1);
  not not_2 (not_2_out, In0);
  not not_3 (not_3_out, Pre0);
  not not_4 (not_4_out, In1);
  not not_5 (not_5_out, Pre0);
  not not_6 (not_6_out, In0);
  not not_7 (not_7_out, Pre1);
  not not_8 (not_8_out, In1);
  not not_9 (not_9_out, In1);
  not not_10 (not_10_out, Pre0);
  not not_11 (not_11_out, In0);
  and and_1 (and_1_out, not_1_out, Pre0, not_2_out);
  or or_1 (Next1, and_1_out, and_2_out, and_3_out);
  and and_2 (and_2_out, Pre1, not_3_out, not_4_out);
  and and_3 (and_3_out, Pre1, not_5_out, not_6_out);
  and and_4 (and_4_out, not_7_out, not_8_out, In0);
  or or_2 (Next0, and_4_out, and_5_out, and_6_out);
  and and_5 (and_5_out, Pre0, not_9_out, In0);
  and and_6 (and_6_out, Pre1, not_10_out, not_11_out);
endmodule

module OutputLogic (
  input  State1,
  input  State0,
  input  In1,
  input  In0,
  output Value
);

  wire not_1_out, not_2_out;

  not not_1 (not_1_out, State0);
  not not_2 (not_2_out, In0);
  and and_1 (Value, State1, not_1_out, not_2_out);
endmodule

module Reset (
  input  Rst,
  input  Clk,
  output out_3
);

  wire register_1_q;

  Register #(.width(1)) register_1 (.D(Rst), .Q(register_1_q), .clk(Clk));  // open: en, clr
  and and_1 (out_3, Rst, register_1_q);
endmodule
