// Logisim project [p3]SingleCycleCPU-AC20171122-144053.circ as structural Verilog: 7 circuits, main circuit main
module main (
  input  Reset,
  output [31:0] out_2,
  output out_3,
  output [4:0] out_4,
  output [31:0] out_5,
  output out_6,
  output [4:0] out_7,
  output [31:0] out_8
);

  wire alu_1_b_bigger, alu_1_b_equal, alu_1_b_smaller, Clk, controlunit_1_alusrc_srcb, controlunit_1_men2reg,
       controlunit_1_regdst, multiplexer_2_out;
  wire [1:0] controlunit_1_branch0, controlunit_1_extop0;
  wire [2:0] controlunit_1_aluctrl0;
  wire [4:0] MemAddr, RegAddr;
  wire [31:0] alu_1_aluresult, dm_1_rd, extu_1_immout, grf_1_rd1, MemData, multiplexer_1_out, RegData;

  IFU ifu_1 (.Instruction(out_2), .Reset(Reset), .PCSrc(multiplexer_2_out), .Clk(Clk));
  ControlUnit controlunit_1 (
    .Op5(out_2[31]), .Op4(out_2[30]), .Op3(out_2[29]), .Op2(out_2[28]), .Op1(out_2[27]), .Op0(out_2[26]),
    .Funct5(out_2[5]), .Funct4(out_2[4]), .Funct3(out_2[3]), .Funct2(out_2[2]), .Funct1(out_2[1]),
    .Funct0(out_2[0]), .RegWriteEN(out_3), .RegDst(controlunit_1_regdst), .ExtOp1(controlunit_1_extop0[1]),
    .ExtOp0(controlunit_1_extop0[0]), .ALUSrc_SrcB(controlunit_1_alusrc_srcb),
    .ALUCtrl2(controlunit_1_aluctrl0[2]), .ALUCtrl1(controlunit_1_aluctrl0[1]),
    .ALUCtrl0(controlunit_1_aluctrl0[0]), .Branch0(controlunit_1_branch0[0]), .MenWrite(out_6),
    .Men2Reg(controlunit_1_men2reg), .Branch1(controlunit_1_branch0[1]));
  GRF grf_1 (
    .Clk(Clk), .WE(out_3), .A1_25_21__rs(out_2[25:21]), .A2_20_16__rt(out_2[20:16]), ._15_11(out_2[15:11]),
    .WD3(RegData), .RegDst_A3(controlunit_1_regdst), .Reset(Reset), .RD1(grf_1_rd1), .RD1_2(MemData),
    .RegAddr(RegAddr));
  ExtU extu_1 (.ImmIn(out_2[15:0]), .ImmOut(extu_1_immout), .ExtOP(controlunit_1_extop0));
  Multiplexer #(.width(32), .enable("false")) multiplexer_1 (
    .in0(MemData), .in1(extu_1_immout), .out(multiplexer_1_out), .sel(controlunit_1_alusrc_srcb));
  ALU alu_1 (
    .SrcA(grf_1_rd1), .SrcB(multiplexer_1_out), .B_equal(alu_1_b_equal), .ALUResult(alu_1_aluresult),
    .ALUCtrl(controlunit_1_aluctrl0), .B_bigger(alu_1_b_bigger), .B_smaller(alu_1_b_smaller));
  Multiplexer #(.select(2), .enable("false")) multiplexer_2 (
    .in0(1'b0), .in1(alu_1_b_equal), .in2(alu_1_b_bigger), .in3(alu_1_b_smaller), .out(multiplexer_2_out),
    .sel(controlunit_1_branch0));
  DM dm_1 (
    .ALUResult_Addr(alu_1_aluresult), .RD2_WD(MemData), .RD(dm_1_rd), .WE(out_6), .Clk(Clk), .Reset(Reset),
    .MemAddr(MemAddr));
  Multiplexer #(.width(32), .disabled(0), .enable("false")) multiplexer_3 (
    .in0(alu_1_aluresult), .in1(dm_1_rd), .out(RegData), .sel(controlunit_1_men2reg));
  Multiplexer #(.width(5), .enable("false")) multiplexer_4 (.in0({5{1'b0}}), .in1(RegAddr), .out(out_4), .sel(out_3));
  Multiplexer #(.width(32), .enable("false")) multiplexer_5 (.in0({32{1'b0}}), .in1(RegData), .out(out_5), .sel(out_3));
  Multiplexer #(.width(5), .enable("false")) multiplexer_6 (.in0({5{1'b0}}), .in1(MemAddr), .out(out_7), .sel(out_6));
  Clock clock_1 (.out(Clk));
  Multiplexer #(.width(32), .enable("false")) multiplexer_7 (.in0({32{1'b0}}), .in1(MemData), .out(out_8), .sel(out_6));

  // Other names for the same wires on the sheet: Instr[31:0] = out_2; MenWrite = out_6; RegWrite = out_3
endmodule

module IFU (
  input  PCSrc,
  input  Reset,
  input  Clk,
  output [31:0] Instruction
);

  wire [31:0] adder_1_out, adder_2_out, bit_extender_1_out, multiplexer_1_out, PC_q;

  Multiplexer #(.width(32), .enable("false")) multiplexer_1 (
    .in0(adder_1_out), .in1(adder_2_out), .out(multiplexer_1_out), .sel(PCSrc));
  Register #(.width(32)) PC (.D(multiplexer_1_out), .Q(PC_q), .clk(Clk), .clr(Reset));  // open: en
  Adder #(.width(32)) adder_1 (.a(PC_q), .b(32'h1), .out(adder_1_out));  // open: cin, cout
  ROM #(.addrWidth(5), .dataWidth(32)) rom_1 (.addr(PC_q[4:0]), .data(Instruction));  // open: sel
  assign bit_extender_1_out = {{16{Instruction[15]}}, Instruction[15:0]};  // Bit_Extender bit_extender_1
  Adder #(.width(32)) adder_2 (.a(bit_extender_1_out), .b(adder_1_out), .out(adder_2_out));  // open: cin, cout

  // Notes on the sheet:
  //   contents of rom_1 (hex, n*v repeats v):
  //   3c100014 3c110010 3c0f0007 f6821 2115021 354a00d8 ac010004 ac0a0064 0 3c1301c7 8c140064 26aa023
  //   11edfff6 3c0f0008
endmodule

module GRF (
  input  Clk,
  input  WE,
  input  [4:0] A1_25_21__rs,
  input  [4:0] A2_20_16__rt,
  input  [4:0] _15_11,
  input  [31:0] WD3,
  input  RegDst_A3,
  input  Reset,
  output [31:0] RD1,
  output [4:0] RegAddr,
  output [31:0] RD1_2
);

  wire and_1_out, and_2_out, and_3_out, and_4_out, and_5_out, and_6_out, and_7_out, and_8_out, and_9_out,
       and_10_out, and_11_out, and_12_out, and_13_out, and_14_out, and_15_out, and_16_out, and_17_out,
       and_18_out, and_19_out, and_20_out, and_21_out, and_22_out, and_23_out, and_24_out, and_25_out,
       and_26_out, and_27_out, and_28_out, and_29_out, and_30_out, and_31_out, w1, w2, w3, w4, w5, w6, w7,
       w8, w9, w10, w11, w12, w13, w14, w15, w16, w17, w18, w19, w20, w21, w22, w23, w24, w25, w26, w27, w28,
       w29, w30, w31;
  wire [31:0] rd_1, rd_2, rd_3, rd_4, rd_5, rd_6, rd_7, rd_8, rd_9, rd_10, rd_11, rd_12, rd_13, rd_14, rd_15,
       rd_16, rd_17, rd_18, rd_19, rd_20, rd_21, rd_22, rd_23, rd_24, rd_25, rd_26, rd_27, rd_28, rd_29,
       rd_30, rd_31;

  Register #(.width(32)) _8 (.D(WD3), .en(and_1_out), .Q(rd_8), .clk(Clk), .clr(Reset));
  and and_1 (and_1_out, w8, WE);
  Register #(.width(32)) _16 (.D(WD3), .en(and_2_out), .Q(rd_16), .clk(Clk), .clr(Reset));
  and and_2 (and_2_out, w16, WE);
  Register #(.width(32)) _24 (.D(WD3), .en(and_3_out), .Q(rd_24), .clk(Clk), .clr(Reset));
  and and_3 (and_3_out, w24, WE);
  Multiplexer #(.width(5), .enable("false")) multiplexer_1 (
    .in0(A2_20_16__rt), .in1(_15_11), .out(RegAddr), .sel(RegDst_A3));
  and and_4 (and_4_out, w1, WE);
  and and_5 (and_5_out, w9, WE);
  and and_6 (and_6_out, w17, WE);
  and and_7 (and_7_out, w25, WE);
  Decoder #(.select(5), .enable("false")) decoder_1 (
    .out1(w1), .out2(w2), .out3(w3), .out4(w4), .out5(w5), .out6(w6), .out7(w7), .out8(w8), .out9(w9),
    .out10(w10), .out11(w11), .out12(w12), .out13(w13), .out14(w14), .out15(w15), .out16(w16), .out17(w17),
    .out18(w18), .out19(w19), .out20(w20), .out21(w21), .out22(w22), .out23(w23), .out24(w24), .out25(w25),
    .out26(w26), .out27(w27), .out28(w28), .out29(w29), .out30(w30), .out31(w31), .sel(RegAddr));  // open: out0
  Register #(.width(32)) _1 (.D(WD3), .en(and_4_out), .Q(rd_1), .clk(Clk), .clr(Reset));
  Register #(.width(32)) _9 (.D(WD3), .en(and_5_out), .Q(rd_9), .clk(Clk), .clr(Reset));
  Register #(.width(32)) _17 (.D(WD3), .en(and_6_out), .Q(rd_17), .clk(Clk), .clr(Reset));
  Register #(.width(32)) _25 (.D(WD3), .en(and_7_out), .Q(rd_25), .clk(Clk), .clr(Reset));
  and and_8 (and_8_out, w2, WE);
  and and_9 (and_9_out, w10, WE);
  and and_10 (and_10_out, w18, WE);
  and and_11 (and_11_out, w26, WE);
  Register #(.width(32)) _2 (.D(WD3), .en(and_8_out), .Q(rd_2), .clk(Clk), .clr(Reset));
  Register #(.width(32)) _10 (.D(WD3), .en(and_9_out), .Q(rd_10), .clk(Clk), .clr(Reset));
  Register #(.width(32)) _18 (.D(WD3), .en(and_10_out), .Q(rd_18), .clk(Clk), .clr(Reset));
  Register #(.width(32)) _26 (.D(WD3), .en(and_11_out), .Q(rd_26), .clk(Clk), .clr(Reset));
  and and_12 (and_12_out, w3, WE);
  and and_13 (and_13_out, w11, WE);
  and and_14 (and_14_out, w19, WE);
  and and_15 (and_15_out, w27, WE);
  Register #(.width(32)) _3 (.D(WD3), .en(and_12_out), .Q(rd_3), .clk(Clk), .clr(Reset));
  Register #(.width(32)) _11 (.D(WD3), .en(and_13_out), .Q(rd_11), .clk(Clk), .clr(Reset));
  Register #(.width(32)) _19 (.D(WD3), .en(and_14_out), .Q(rd_19), .clk(Clk), .clr(Reset));
  Register #(.width(32)) _27 (.D(WD3), .en(and_15_out), .Q(rd_27), .clk(Clk), .clr(Reset));
  and and_16 (and_16_out, w4, WE);
  and and_17 (and_17_out, w12, WE);
  and and_18 (and_18_out, w20, WE);
  and and_19 (and_19_out, w28, WE);
  Register #(.width(32)) _4 (.D(WD3), .en(and_16_out), .Q(rd_4), .clk(Clk), .clr(Reset));
  Register #(.width(32)) _12 (.D(WD3), .en(and_17_out), .Q(rd_12), .clk(Clk), .clr(Reset));
  Register #(.width(32)) _20 (.D(WD3), .en(and_18_out), .Q(rd_20), .clk(Clk), .clr(Reset));
  Register #(.width(32)) _28 (.D(WD3), .en(and_19_out), .Q(rd_28), .clk(Clk), .clr(Reset));
  Register #(.width(32)) _5 (.D(WD3), .en(and_20_out), .Q(rd_5), .clk(Clk), .clr(Reset));
  and and_20 (and_20_out, w5, WE);
  Register #(.width(32)) _13 (.D(WD3), .en(and_21_out), .Q(rd_13), .clk(Clk), .clr(Reset));
  and and_21 (and_21_out, w13, WE);
  Register #(.width(32)) _21 (.D(WD3), .en(and_22_out), .Q(rd_21), .clk(Clk), .clr(Reset));
  and and_22 (and_22_out, w21, WE);
  Register #(.width(32)) _29 (.D(WD3), .en(and_23_out), .Q(rd_29), .clk(Clk), .clr(Reset));
  and and_23 (and_23_out, w29, WE);
  Register #(.width(32)) _6 (.D(WD3), .en(and_24_out), .Q(rd_6), .clk(Clk), .clr(Reset));
  and and_24 (and_24_out, w6, WE);
  Register #(.width(32)) _14 (.D(WD3), .en(and_25_out), .Q(rd_14), .clk(Clk), .clr(Reset));
  and and_25 (and_25_out, w14, WE);
  Register #(.width(32)) _22 (.D(WD3), .en(and_26_out), .Q(rd_22), .clk(Clk), .clr(Reset));
  and and_26 (and_26_out, w22, WE);
  Register #(.width(32)) _30 (.D(WD3), .en(and_27_out), .Q(rd_30), .clk(Clk), .clr(Reset));
  and and_27 (and_27_out, w30, WE);
  Register #(.width(32)) _7 (.D(WD3), .en(and_28_out), .Q(rd_7), .clk(Clk), .clr(Reset));
  and and_28 (and_28_out, w7, WE);
  Register #(.width(32)) _15 (.D(WD3), .en(and_29_out), .Q(rd_15), .clk(Clk), .clr(Reset));
  and and_29 (and_29_out, w15, WE);
  Register #(.width(32)) _23 (.D(WD3), .en(and_30_out), .Q(rd_23), .clk(Clk), .clr(Reset));
  and and_30 (and_30_out, w23, WE);
  Register #(.width(32)) _31 (.D(WD3), .en(and_31_out), .Q(rd_31), .clk(Clk), .clr(Reset));
  and and_31 (and_31_out, w31, WE);
  Multiplexer #(.select(5), .width(32), .disabled(0), .enable("false")) multiplexer_2 (
    .in0({32{1'b0}}), .in1(rd_1), .in2(rd_2), .in3(rd_3), .in4(rd_4), .in5(rd_5), .in6(rd_6), .in7(rd_7),
    .in8(rd_8), .in9(rd_9), .in10(rd_10), .in11(rd_11), .in12(rd_12), .in13(rd_13), .in14(rd_14),
    .in15(rd_15), .in16(rd_16), .in17(rd_17), .in18(rd_18), .in19(rd_19), .in20(rd_20), .in21(rd_21),
    .in22(rd_22), .in23(rd_23), .in24(rd_24), .in25(rd_25), .in26(rd_26), .in27(rd_27), .in28(rd_28),
    .in29(rd_29), .in30(rd_30), .in31(rd_31), .out(RD1), .sel(A1_25_21__rs));
  Multiplexer #(.select(5), .width(32), .disabled(0), .enable("false")) multiplexer_3 (
    .in0({32{1'b0}}), .in1(rd_1), .in2(rd_2), .in3(rd_3), .in4(rd_4), .in5(rd_5), .in6(rd_6), .in7(rd_7),
    .in8(rd_8), .in9(rd_9), .in10(rd_10), .in11(rd_11), .in12(rd_12), .in13(rd_13), .in14(rd_14),
    .in15(rd_15), .in16(rd_16), .in17(rd_17), .in18(rd_18), .in19(rd_19), .in20(rd_20), .in21(rd_21),
    .in22(rd_22), .in23(rd_23), .in24(rd_24), .in25(rd_25), .in26(rd_26), .in27(rd_27), .in28(rd_28),
    .in29(rd_29), .in30(rd_30), .in31(rd_31), .out(RD1_2), .sel(A2_20_16__rt));

  // Other names for the same wires on the sheet: A1[4:0] = A1_25_21__rs; A2[4:0] = A2_20_16__rt
endmodule

module ALU (
  input  [2:0] ALUCtrl,
  input  [31:0] SrcA,
  input  [31:0] SrcB,
  output B_bigger,
  output B_equal,
  output B_smaller,
  output [31:0] ALUResult
);

  wire [31:0] adder_1_out, and_1_out, or_1_out, subtractor_1_out;

  Adder #(.width(32)) adder_1 (.a(SrcA), .b(SrcB), .out(adder_1_out));  // open: cin, cout
  Subtractor #(.width(32)) subtractor_1 (.a(SrcA), .b(SrcB), .out(subtractor_1_out));  // open: bin, bout
  assign or_1_out = SrcA | SrcB;  // OR_Gate or_1, 32 bits wide
  assign and_1_out = SrcA & SrcB;  // AND_Gate and_1, 32 bits wide
  Multiplexer #(.select(3), .width(32), .enable("false")) multiplexer_1 (
    .in0(adder_1_out), .in1(subtractor_1_out), .in2(or_1_out), .in3(and_1_out), .out(ALUResult), .sel(ALUCtrl));  // open: in4, in5, in6, in7
  Comparator #(.width(32), .mode("unsigned")) comparator_1 (
    .a(ALUResult), .b({32{1'b0}}), .gt(B_bigger), .eq(B_equal), .lt(B_smaller));
endmodule

module DM (
  input  [31:0] ALUResult_Addr,
  input  WE,
  input  Clk,
  input  Reset,
  input  [31:0] RD2_WD,
  output [4:0] MemAddr,
  output [31:0] RD
);

  wire [31:5] shifter_1_out;

  Shifter #(.width(32), .shift("ar")) shifter_1 (
    .in(ALUResult_Addr), .\dist (5'b00010), .out({shifter_1_out, MemAddr}));
  RAM #(.addrWidth(5), .dataWidth(32), .bus("separate")) ram_1 (
    .addr(MemAddr), .din(RD2_WD), .data(RD), .str(WE), .clk(Clk), .ld(1'b1), .clr(Reset));  // open: sel
endmodule

module ExtU (
  input  [1:0] ExtOP,
  input  [15:0] ImmIn,
  output [31:0] ImmOut
);

  wire [31:0] bit_extender_1_out, bit_extender_2_out, bit_extender_3_out, shifter_1_out;

  assign bit_extender_1_out = {{16{1'b0}}, ImmIn};  // Bit_Extender bit_extender_1
  assign bit_extender_2_out = {{16{ImmIn[15]}}, ImmIn};  // Bit_Extender bit_extender_2
  assign bit_extender_3_out = {{16{1'b0}}, ImmIn};  // Bit_Extender bit_extender_3
  Shifter #(.width(32)) shifter_1 (.in(bit_extender_3_out), .\dist (5'b10000), .out(shifter_1_out));
  Multiplexer #(.select(2), .width(32)) multiplexer_1 (
    .in0(bit_extender_1_out), .in1(bit_extender_2_out), .in2(shifter_1_out), .out(ImmOut), .sel(ExtOP));  // open: in3, en
endmodule

module ControlUnit (
  input  Op5,
  input  Op4,
  input  Op3,
  input  Op2,
  input  Op1,
  input  Op0,
  input  Funct5,
  input  Funct4,
  input  Funct3,
  input  Funct2,
  input  Funct1,
  input  Funct0,
  output RegWriteEN,
  output RegDst,
  output ExtOp1,
  output ExtOp0,
  output ALUSrc_SrcB,
  output ALUCtrl2,
  output ALUCtrl1,
  output ALUCtrl0,
  output Branch1,
  output Branch0,
  output MenWrite,
  output Men2Reg
);

  wire addu_out, beq_out, lui_out, lw_out, not_1_out, not_2_out, not_3_out, not_4_out, not_5_out, not_6_out,
       not_7_out, not_8_out, not_9_out, not_10_out, not_11_out, not_12_out, ori_out, subu_out, sw_out;

  not not_1 (not_1_out, Op5);
  not not_2 (not_2_out, Op3);
  not not_3 (not_3_out, Op4);
  not not_4 (not_4_out, Op2);
  not not_5 (not_5_out, Op1);
  not not_6 (not_6_out, Op0);
  not not_7 (not_7_out, Funct5);
  not not_8 (not_8_out, Funct3);
  not not_9 (not_9_out, Funct4);
  not not_10 (not_10_out, Funct1);
  not not_11 (not_11_out, Funct2);
  not not_12 (not_12_out, Funct0);
  and addu (addu_out, not_6_out, not_5_out, not_4_out, not_2_out, not_3_out, not_1_out, Funct0, not_10_out, not_11_out, not_8_out, not_9_out, Funct5);
  and subu (subu_out, not_6_out, not_5_out, not_4_out, not_2_out, not_3_out, not_1_out, Funct0, Funct1, not_11_out, not_8_out, not_9_out, Funct5);
  and ori (ori_out, Op0, not_5_out, Op2, Op3, not_3_out, not_1_out);
  and lw (lw_out, Op0, Op1, not_4_out, not_2_out, not_3_out, Op5);
  and sw (sw_out, Op0, Op1, not_4_out, Op3, not_3_out, Op5);
  and beq (beq_out, not_6_out, not_5_out, Op2, not_2_out, not_3_out, not_1_out);
  and lui (lui_out, Op0, Op1, Op2, Op3, not_3_out, not_1_out);
  or or_1 (RegWriteEN, lui_out, addu_out, subu_out, ori_out, lw_out);
  or or_2 (RegDst, addu_out, subu_out);
  buf or_3 (ExtOp1, lui_out);  // OR_Gate
  or or_4 (ExtOp0, lw_out, sw_out, beq_out);
  or or_5 (ALUSrc_SrcB, ori_out, lw_out, sw_out, lui_out);
  buf or_6 (ALUCtrl2, 1'b0);  // OR_Gate
  or or_7 (ALUCtrl1, 1'b0, ori_out, lui_out);
  or or_8 (ALUCtrl0, 1'b0, subu_out, beq_out);
  buf or_9 (Branch1, 1'b0);  // OR_Gate
  buf or_10 (Branch0, beq_out);  // OR_Gate
  buf or_11 (MenWrite, sw_out);  // OR_Gate
  buf or_12 (Men2Reg, lw_out);  // OR_Gate
endmodule
