// Logisim project [p3]SingleCycleCPU-Final(39instructions).circ as structural Verilog: 7 circuits, main circuit main
module main (
  input  Reset,
  output [31:0] out_2,
  output out_3,
  output [4:0] out_4,
  output [31:0] out_5,
  output out_6,
  output [4:0] out_7,
  output [31:0] out_8
);

  wire alu_1_b_bigger, alu_1_b_equal, alu_1_b_smaller, and_1_out, and_2_out, and_3_out, Clk,
       controlunit_1_alusrc_srcb, controlunit_1_j_jal, controlunit_1_j_type, controlunit_1_jarl,
       controlunit_1_men2reg, multiplexer_5_out, not_1_out, not_2_out, not_3_out, not_4_out, not_5_out,
       or_1_out, or_2_out, or_3_out, or_4_out;
  wire [1:0] controlunit_1_extop0, controlunit_1_regdst0;
  wire [2:0] controlunit_1_branch0, controlunit_1_load0;
  wire [3:0] controlunit_1_aluctrl0;
  wire [4:0] MemAddr, RegAddr;
  wire [5:0] RealFunc;
  wire [31:0] alu_1_aluresult, dm_1_rd, extu_1_immout, grf_1_rd1, ifu_1_pc_4, MemData, multiplexer_1_out,
       multiplexer_3_out, multiplexer_4_out, RegData;

  IFU ifu_1 (
    .Instruction(out_2), .Reset(Reset), .PCSrc(multiplexer_5_out), .Clk(Clk), .J_Type(controlunit_1_j_type),
    .JumpAddr(grf_1_rd1), .J_Jal(controlunit_1_j_jal), .PC_4(ifu_1_pc_4));
  or or_1 (or_1_out, controlunit_1_j_jal, controlunit_1_jarl);
  Multiplexer #(.width(32), .enable("false")) multiplexer_1 (
    .in0(RegData), .in1(ifu_1_pc_4), .out(multiplexer_1_out), .sel(or_1_out));
  ControlUnit controlunit_1 (
    .Op5(out_2[31]), .Op4(out_2[30]), .Op3(out_2[29]), .Op2(out_2[28]), .Op1(out_2[27]), .Op0(out_2[26]),
    .Funct5(RealFunc[5]), .Funct4(RealFunc[4]), .Funct3(RealFunc[3]), .Funct2(RealFunc[2]),
    .Funct1(RealFunc[1]), .Funct0(RealFunc[0]), .RegWriteEN(out_3), .RegDst0(controlunit_1_regdst0[0]),
    .ExtOp1(controlunit_1_extop0[1]), .ExtOp0(controlunit_1_extop0[0]),
    .ALUSrc_SrcB(controlunit_1_alusrc_srcb), .ALUCtrl2(controlunit_1_aluctrl0[2]),
    .ALUCtrl1(controlunit_1_aluctrl0[1]), .ALUCtrl0(controlunit_1_aluctrl0[0]),
    .Branch0(controlunit_1_branch0[0]), .MenWrite(out_6), .Men2Reg(controlunit_1_men2reg),
    .Branch1(controlunit_1_branch0[1]), .RegDst1(controlunit_1_regdst0[1]), .J_Type(controlunit_1_j_type),
    .J_Jal(controlunit_1_j_jal), .Load0(controlunit_1_load0[0]), .Load1(controlunit_1_load0[1]),
    .Load2(controlunit_1_load0[2]), .Branch2(controlunit_1_branch0[2]), .ALUCtrl3(controlunit_1_aluctrl0[3]),
    .Jarl(controlunit_1_jarl));
  Multiplexer #(.width(6), .enable("false")) multiplexer_2 (
    .in0(out_2[5:0]), .in1({1'b0, out_2[20:16]}), .out(RealFunc), .sel(and_2_out));
  GRF grf_1 (
    .Clk(Clk), .WE(out_3), .A1_25_21__rs(out_2[25:21]), .A2_20_16__rt(out_2[20:16]), ._15_11(out_2[15:11]),
    .WD3(multiplexer_1_out), .RegDst_A3(controlunit_1_regdst0), .Reset(Reset), .RD1(grf_1_rd1),
    .RD2(MemData), .RegAddr(RegAddr));
  ExtU extu_1 (.ImmIn(out_2[15:0]), .ImmOut(extu_1_immout), .ExtOP(controlunit_1_extop0));
  not not_1 (not_1_out, out_2[27]);
  not not_2 (not_2_out, out_2[28]);
  not not_3 (not_3_out, out_2[29]);
  not not_4 (not_4_out, out_2[30]);
  not not_5 (not_5_out, out_2[31]);
  Multiplexer #(.width(32), .enable("false")) multiplexer_3 (
    .in0(MemData), .in1(extu_1_immout), .out(multiplexer_3_out), .sel(controlunit_1_alusrc_srcb));
  and and_1 (and_1_out, out_2[26], not_1_out, not_2_out);
  and and_2 (and_2_out, and_1_out, and_3_out);
  and and_3 (and_3_out, not_3_out, not_4_out, not_5_out);
  Multiplexer #(.width(32), .enable("false")) multiplexer_4 (
    .in0(multiplexer_3_out), .in1({32{1'b0}}), .out(multiplexer_4_out), .sel(and_2_out));
  ALU alu_1 (
    .SrcA(grf_1_rd1), .SrcB(multiplexer_4_out), .B_equal(alu_1_b_equal), .ALUResult(alu_1_aluresult),
    .ALUCtrl(controlunit_1_aluctrl0), .B_bigger(alu_1_b_bigger), .B_smaller(alu_1_b_smaller),
    .Shift(out_2[10:6]));
  or or_2 (or_2_out, alu_1_b_bigger, alu_1_b_equal);
  or or_3 (or_3_out, alu_1_b_equal, alu_1_b_smaller);
  or or_4 (or_4_out, alu_1_b_bigger, alu_1_b_smaller);
  Multiplexer #(.select(3), .enable("false")) multiplexer_5 (
    .in0(1'b0), .in1(alu_1_b_equal), .in2(or_2_out), .in3(alu_1_b_bigger), .in4(or_3_out),
    .in5(alu_1_b_smaller), .in6(or_4_out), .out(multiplexer_5_out), .sel(controlunit_1_branch0));  // open: in7
  DM dm_1 (
    .ALUResult_Addr(alu_1_aluresult), .RD2_WD(MemData), .RD(dm_1_rd), .WE(out_6), .Clk(Clk), .Reset(Reset),
    .MemAddr(MemAddr), .Load(controlunit_1_load0));
  Multiplexer #(.width(32), .disabled(0), .enable("false")) multiplexer_6 (
    .in0(alu_1_aluresult), .in1(dm_1_rd), .out(RegData), .sel(controlunit_1_men2reg));
  Multiplexer #(.width(5), .enable("false")) multiplexer_7 (.in0({5{1'b0}}), .in1(RegAddr), .out(out_4), .sel(out_3));
  Multiplexer #(.width(32), .enable("false")) multiplexer_8 (.in0({32{1'b0}}), .in1(RegData), .out(out_5), .sel(out_3));
  Multiplexer #(.width(5), .enable("false")) multiplexer_9 (.in0({5{1'b0}}), .in1(MemAddr), .out(out_7), .sel(out_6));
  Clock clock_1 (.out(Clk));
  Multiplexer #(.width(32), .enable("false")) multiplexer_10 (
    .in0({32{1'b0}}), .in1(MemData), .out(out_8), .sel(out_6));

  // Other names for the same wires on the sheet: Instr[31:0] = out_2; FuncOriginal[5:0] = out_2[5:0];
  //   MenWrite = out_6; RegWrite = out_3

  // Notes on the sheet:
  //   Bgez/Bltz FuncCode
  //   Bgez/Bltz OPCode
endmodule

module IFU (
  input  PCSrc,
  input  Reset,
  input  Clk,
  input  J_Type,
  input  J_Jal,
  input  [31:0] JumpAddr,
  output [31:0] Instruction,
  output [31:0] PC_4
);

  wire [31:0] adder_2_out, bit_extender_1_out, multiplexer_1_out, multiplexer_2_out, multiplexer_3_out, PC_q,
       shifter_1_out;

  Multiplexer #(.width(32), .enable("false")) multiplexer_1 (
    .in0(multiplexer_2_out), .in1(adder_2_out), .out(multiplexer_1_out), .sel(PCSrc));
  Register #(.width(32)) PC (.D(multiplexer_1_out), .Q(PC_q), .clk(Clk), .clr(Reset));  // open: en
  Multiplexer #(.width(32), .enable("false")) multiplexer_2 (
    .in0(PC_4), .in1(multiplexer_3_out), .out(multiplexer_2_out), .sel(J_Type));
  Multiplexer #(.width(32), .enable("false")) multiplexer_3 (
    .in0(JumpAddr), .in1({PC_q[31:28], Instruction[25:0], 2'b00}), .out(multiplexer_3_out), .sel(J_Jal));
  Adder #(.width(32)) adder_1 (.a(PC_q), .b(32'h4), .out(PC_4));  // open: cin, cout
  ROM #(.addrWidth(5), .dataWidth(32)) rom_1 (.addr(PC_q[6:2]), .data(Instruction));  // open: sel
  assign bit_extender_1_out = {{16{Instruction[15]}}, Instruction[15:0]};  // Bit_Extender bit_extender_1
  Shifter #(.width(32)) shifter_1 (.in(bit_extender_1_out), .\dist (5'b00010), .out(shifter_1_out));
  Adder #(.width(32)) adder_2 (.a(shifter_1_out), .b(PC_4), .out(adder_2_out));  // open: cin, cout

  // Notes on the sheet:
  //   contents of rom_1 (hex, n*v repeats v):
  //   3c08ff88 3c09fa24 1095023 354b1b62 3c0cfa23 b81c0 16b8804 990c3 b9943 16ba007 169a807 8b302 8ba42
endmodule

module GRF (
  input  Clk,
  input  WE,
  input  [4:0] A1_25_21__rs,
  input  [4:0] A2_20_16__rt,
  input  [4:0] _15_11,
  input  [31:0] WD3,
  input  [1:0] RegDst_A3,
  input  Reset,
  output [31:0] RD1,
  output [4:0] RegAddr,
  output [31:0] RD2
);

  wire and_1_out, and_2_out, and_3_out, and_4_out, and_5_out, and_6_out, and_7_out, and_8_out, and_9_out,
       and_10_out, and_11_out, and_12_out, and_13_out, and_14_out, and_15_out, and_16_out, and_17_out,
       and_18_out, and_19_out, and_20_out, and_21_out, and_22_out, and_23_out, and_24_out, and_25_out,
       and_26_out, and_27_out, and_28_out, and_29_out, and_30_out, and_31_out, w1, w2, w3, w4, w5, w6, w7,
       w8, w9, w10, w11, w12, w13, w14, w15, w16, w17, w18, w19, w20, w21, w22, w23, w24, w25, w26, w27, w28,
       w29, w30, w31;
  wire [31:0] rd_1, rd_2, rd_3, rd_4, rd_5, rd_6, rd_7, rd_8, rd_9, rd_10, rd_11, rd_12, rd_13, rd_14, rd_15,
       rd_16, rd_17, rd_18, rd_19, rd_20, rd_21, rd_22, rd_23, rd_24, rd_25, rd_26, rd_27, rd_28, rd_29,
       rd_30, rd_31;

  Register #(.width(32)) _8 (.D(WD3), .en(and_1_out), .Q(rd_8), .clk(Clk), .clr(Reset));
  and and_1 (and_1_out, w8, WE);
  Register #(.width(32)) _16 (.D(WD3), .en(and_2_out), .Q(rd_16), .clk(Clk), .clr(Reset));
  and and_2 (and_2_out, w16, WE);
  Register #(.width(32)) _24 (.D(WD3), .en(and_3_out), .Q(rd_24), .clk(Clk), .clr(Reset));
  and and_3 (and_3_out, w24, WE);
  Multiplexer #(.select(2), .width(5), .enable("false")) multiplexer_1 (
    .in0(A2_20_16__rt), .in1(_15_11), .in2({5{1'b1}}), .in3({5{1'b0}}), .out(RegAddr), .sel(RegDst_A3));
  and and_4 (and_4_out, w1, WE);
  and and_5 (and_5_out, w9, WE);
  and and_6 (and_6_out, w17, WE);
  and and_7 (and_7_out, w25, WE);
  Decoder #(.select(5), .enable("false")) decoder_1 (
    .out1(w1), .out2(w2), .out3(w3), .out4(w4), .out5(w5), .out6(w6), .out7(w7), .out8(w8), .out9(w9),
    .out10(w10), .out11(w11), .out12(w12), .out13(w13), .out14(w14), .out15(w15), .out16(w16), .out17(w17),
    .out18(w18), .out19(w19), .out20(w20), .out21(w21), .out22(w22), .out23(w23), .out24(w24), .out25(w25),
    .out26(w26), .out27(w27), .out28(w28), .out29(w29), .out30(w30), .out31(w31), .sel(RegAddr));  // open: out0
  Register #(.width(32)) _1 (.D(WD3), .en(and_4_out), .Q(rd_1), .clk(Clk), .clr(Reset));
  Register #(.width(32)) _9 (.D(WD3), .en(and_5_out), .Q(rd_9), .clk(Clk), .clr(Reset));
  Register #(.width(32)) _17 (.D(WD3), .en(and_6_out), .Q(rd_17), .clk(Clk), .clr(Reset));
  Register #(.width(32)) _25 (.D(WD3), .en(and_7_out), .Q(rd_25), .clk(Clk), .clr(Reset));
  and and_8 (and_8_out, w2, WE);
  and and_9 (and_9_out, w10, WE);
  and and_10 (and_10_out, w18, WE);
  and and_11 (and_11_out, w26, WE);
  Register #(.width(32)) _2 (.D(WD3), .en(and_8_out), .Q(rd_2), .clk(Clk), .clr(Reset));
  Register #(.width(32)) _10 (.D(WD3), .en(and_9_out), .Q(rd_10), .clk(Clk), .clr(Reset));
  Register #(.width(32)) _18 (.D(WD3), .en(and_10_out), .Q(rd_18), .clk(Clk), .clr(Reset));
  Register #(.width(32)) _26 (.D(WD3), .en(and_11_out), .Q(rd_26), .clk(Clk), .clr(Reset));
  and and_12 (and_12_out, w3, WE);
  and and_13 (and_13_out, w11, WE);
  and and_14 (and_14_out, w19, WE);
  and and_15 (and_15_out, w27, WE);
  Register #(.width(32)) _3 (.D(WD3), .en(and_12_out), .Q(rd_3), .clk(Clk), .clr(Reset));
  Register #(.width(32)) _11 (.D(WD3), .en(and_13_out), .Q(rd_11), .clk(Clk), .clr(Reset));
  Register #(.width(32)) _19 (.D(WD3), .en(and_14_out), .Q(rd_19), .clk(Clk), .clr(Reset));
  Register #(.width(32)) _27 (.D(WD3), .en(and_15_out), .Q(rd_27), .clk(Clk), .clr(Reset));
  and and_16 (and_16_out, w4, WE);
  and and_17 (and_17_out, w12, WE);
  and and_18 (and_18_out, w20, WE);
  and and_19 (and_19_out, w28, WE);
  Register #(.width(32)) _4 (.D(WD3), .en(and_16_out), .Q(rd_4), .clk(Clk), .clr(Reset));
  Register #(.width(32)) _12 (.D(WD3), .en(and_17_out), .Q(rd_12), .clk(Clk), .clr(Reset));
  Register #(.width(32)) _20 (.D(WD3), .en(and_18_out), .Q(rd_20), .clk(Clk), .clr(Reset));
  Register #(.width(32)) _28 (.D(WD3), .en(and_19_out), .Q(rd_28), .clk(Clk), .clr(Reset));
  Register #(.width(32)) _5 (.D(WD3), .en(and_20_out), .Q(rd_5), .clk(Clk), .clr(Reset));
  and and_20 (and_20_out, w5, WE);
  Register #(.width(32)) _13 (.D(WD3), .en(and_21_out), .Q(rd_13), .clk(Clk), .clr(Reset));
  and and_21 (and_21_out, w13, WE);
  Register #(.width(32)) _21 (.D(WD3), .en(and_22_out), .Q(rd_21), .clk(Clk), .clr(Reset));
  and and_22 (and_22_out, w21, WE);
  Register #(.width(32)) _29 (.D(WD3), .en(and_23_out), .Q(rd_29), .clk(Clk), .clr(Reset));
  and and_23 (and_23_out, w29, WE);
  Register #(.width(32)) _6 (.D(WD3), .en(and_24_out), .Q(rd_6), .clk(Clk), .clr(Reset));
  and and_24 (and_24_out, w6, WE);
  Register #(.width(32)) _14 (.D(WD3), .en(and_25_out), .Q(rd_14), .clk(Clk), .clr(Reset));
  and and_25 (and_25_out, w14, WE);
  Register #(.width(32)) _22 (.D(WD3), .en(and_26_out), .Q(rd_22), .clk(Clk), .clr(Reset));
  and and_26 (and_26_out, w22, WE);
  Register #(.width(32)) _30 (.D(WD3), .en(and_27_out), .Q(rd_30), .clk(Clk), .clr(Reset));
  and and_27 (and_27_out, w30, WE);
  Register #(.width(32)) _7 (.D(WD3), .en(and_28_out), .Q(rd_7), .clk(Clk), .clr(Reset));
  and and_28 (and_28_out, w7, WE);
  Register #(.width(32)) _15 (.D(WD3), .en(and_29_out), .Q(rd_15), .clk(Clk), .clr(Reset));
  and and_29 (and_29_out, w15, WE);
  Register #(.width(32)) _23 (.D(WD3), .en(and_30_out), .Q(rd_23), .clk(Clk), .clr(Reset));
  and and_30 (and_30_out, w23, WE);
  Register #(.width(32)) _31 (.D(WD3), .en(and_31_out), .Q(rd_31), .clk(Clk), .clr(Reset));
  and and_31 (and_31_out, w31, WE);
  Multiplexer #(.select(5), .width(32), .disabled(0), .enable("false")) multiplexer_2 (
    .in0({32{1'b0}}), .in1(rd_1), .in2(rd_2), .in3(rd_3), .in4(rd_4), .in5(rd_5), .in6(rd_6), .in7(rd_7),
    .in8(rd_8), .in9(rd_9), .in10(rd_10), .in11(rd_11), .in12(rd_12), .in13(rd_13), .in14(rd_14),
    .in15(rd_15), .in16(rd_16), .in17(rd_17), .in18(rd_18), .in19(rd_19), .in20(rd_20), .in21(rd_21),
    .in22(rd_22), .in23(rd_23), .in24(rd_24), .in25(rd_25), .in26(rd_26), .in27(rd_27), .in28(rd_28),
    .in29(rd_29), .in30(rd_30), .in31(rd_31), .out(RD1), .sel(A1_25_21__rs));
  Multiplexer #(.select(5), .width(32), .disabled(0), .enable("false")) multiplexer_3 (
    .in0({32{1'b0}}), .in1(rd_1), .in2(rd_2), .in3(rd_3), .in4(rd_4), .in5(rd_5), .in6(rd_6), .in7(rd_7),
    .in8(rd_8), .in9(rd_9), .in10(rd_10), .in11(rd_11), .in12(rd_12), .in13(rd_13), .in14(rd_14),
    .in15(rd_15), .in16(rd_16), .in17(rd_17), .in18(rd_18), .in19(rd_19), .in20(rd_20), .in21(rd_21),
    .in22(rd_22), .in23(rd_23), .in24(rd_24), .in25(rd_25), .in26(rd_26), .in27(rd_27), .in28(rd_28),
    .in29(rd_29), .in30(rd_30), .in31(rd_31), .out(RD2), .sel(A2_20_16__rt));

  // Other names for the same wires on the sheet: A1[4:0] = A1_25_21__rs; A2[4:0] = A2_20_16__rt
endmodule

module ALU (
  input  [3:0] ALUCtrl,
  input  [31:0] SrcA,
  input  [31:0] SrcB,
  input  [4:0] Shift,
  output B_bigger,
  output B_equal,
  output B_smaller,
  output [31:0] ALUResult
);

  wire [0:0] comparator_1_lt, comparator_2_lt;
  wire [31:0] adder_1_out, and_1_out, nor_1_out, or_1_out, shifter_1_out, shifter_2_out, shifter_3_out,
       shifter_4_out, shifter_5_out, shifter_6_out, subtractor_1_out, xor_1_out;

  Adder #(.width(32)) adder_1 (.a(SrcA), .b(SrcB), .out(adder_1_out));  // open: cin, cout
  Subtractor #(.width(32)) subtractor_1 (.a(SrcA), .b(SrcB), .out(subtractor_1_out));  // open: bin, bout
  assign or_1_out = SrcA | SrcB;  // OR_Gate or_1, 32 bits wide
  assign and_1_out = SrcA & SrcB;  // AND_Gate and_1, 32 bits wide
  assign nor_1_out = ~(SrcA | SrcB);  // NOR_Gate nor_1, 32 bits wide
  assign xor_1_out = SrcA ^ SrcB;  // XOR_Gate xor_1, 32 bits wide
  Comparator #(.width(32)) comparator_1 (.a(SrcA), .b(SrcB), .lt(comparator_1_lt[0]));  // open: gt, eq
  Comparator #(.width(32), .mode("unsigned")) comparator_2 (
    .a(SrcA), .b(SrcB), .lt(comparator_2_lt[0]));  // open: gt, eq
  Shifter #(.width(32)) shifter_1 (.in(SrcB), .\dist (Shift), .out(shifter_1_out));
  Shifter #(.width(32)) shifter_2 (.in(SrcB), .\dist (SrcA[4:0]), .out(shifter_2_out));
  Shifter #(.width(32), .shift("ar")) shifter_3 (.in(SrcB), .\dist (Shift), .out(shifter_3_out));
  Shifter #(.width(32), .shift("ar")) shifter_4 (.in(SrcB), .\dist (SrcA[4:0]), .out(shifter_4_out));
  Shifter #(.width(32), .shift("lr")) shifter_5 (.in(SrcB), .\dist (Shift), .out(shifter_5_out));
  Shifter #(.width(32), .shift("lr")) shifter_6 (.in(SrcB), .\dist (SrcA[4:0]), .out(shifter_6_out));
  Multiplexer #(.select(4), .width(32), .enable("false")) multiplexer_1 (
    .in0(adder_1_out), .in1(subtractor_1_out), .in2(or_1_out), .in3(and_1_out), .in4(nor_1_out),
    .in5(xor_1_out), .in6({{31{1'b0}}, comparator_1_lt[0]}), .in7({{31{1'b0}}, comparator_2_lt[0]}),
    .in8(shifter_1_out), .in9(shifter_2_out), .in10(shifter_3_out), .in11(shifter_4_out),
    .in12(shifter_5_out), .in13(shifter_6_out), .out(ALUResult), .sel(ALUCtrl));  // open: in14, in15
  Comparator #(.width(32)) comparator_3 (.a(ALUResult), .b({32{1'b0}}), .gt(B_bigger), .eq(B_equal), .lt(B_smaller));
endmodule

module DM (
  input  [2:0] Load,
  input  [31:0] ALUResult_Addr,
  input  WE,
  input  Clk,
  input  Reset,
  input  [31:0] RD2_WD,
  output [4:0] MemAddr,
  output [31:0] RD
);

  wire [7:0] multiplexer_5_out, ram_1_data, ram_1_data_2, ram_1_data_3;
  wire [15:0] multiplexer_4_out;
  wire [31:0] bit_extender_1_out, bit_extender_2_out, multiplexer_1_out, multiplexer_2_out, multiplexer_3_out;
  wire [31:5] shifter_1_out;
  wire [31:24] ram_1_data_4;

  Shifter #(.width(32), .shift("ar")) shifter_1 (
    .in(ALUResult_Addr), .\dist (5'b00010), .out({shifter_1_out, MemAddr}));
  Multiplexer #(.width(32), .enable("false")) multiplexer_1 (
    .in0({ram_1_data_4, ram_1_data_3, RD2_WD[15:0]}), .in1({RD2_WD[15:0], ram_1_data_2, ram_1_data}),
    .out(multiplexer_1_out), .sel(ALUResult_Addr[1]));
  Multiplexer #(.select(3), .width(32), .enable("false")) multiplexer_2 (
    .in0(RD2_WD), .in1(multiplexer_1_out), .in2(multiplexer_3_out), .out(multiplexer_2_out), .sel(Load));  // open: in3, in4, in5, in6, in7
  Multiplexer #(.select(2), .width(32), .enable("false")) multiplexer_3 (
    .in0({ram_1_data_4, ram_1_data_3, ram_1_data_2, RD2_WD[7:0]}),
    .in1({ram_1_data_4, ram_1_data_3, RD2_WD[7:0], ram_1_data}),
    .in2({ram_1_data_4, RD2_WD[7:0], ram_1_data_2, ram_1_data}),
    .in3({RD2_WD[7:0], ram_1_data_3, ram_1_data_2, ram_1_data}), .out(multiplexer_3_out),
    .sel(ALUResult_Addr[1:0]));
  RAM #(.addrWidth(5), .dataWidth(32), .bus("separate")) ram_1 (
    .addr(MemAddr), .din(multiplexer_2_out), .data({ram_1_data_4, ram_1_data_3, ram_1_data_2, ram_1_data}),
    .str(WE), .clk(Clk), .ld(1'b1), .clr(Reset));  // open: sel
  Multiplexer #(.width(16), .enable("false")) multiplexer_4 (
    .in0({ram_1_data_2, ram_1_data}), .in1({ram_1_data_4, ram_1_data_3}), .out(multiplexer_4_out),
    .sel(ALUResult_Addr[1]));
  assign bit_extender_1_out = {{16{multiplexer_4_out[15]}}, multiplexer_4_out};  // Bit_Extender bit_extender_1
  Multiplexer #(.select(2), .width(8), .enable("false")) multiplexer_5 (
    .in0(ram_1_data), .in1(ram_1_data_2), .in2(ram_1_data_3), .in3(ram_1_data_4), .out(multiplexer_5_out),
    .sel(ALUResult_Addr[1:0]));
  assign bit_extender_2_out = {{24{multiplexer_5_out[7]}}, multiplexer_5_out};  // Bit_Extender bit_extender_2
  Multiplexer #(.select(3), .width(32), .enable("false")) multiplexer_6 (
    .in0({ram_1_data_4, ram_1_data_3, ram_1_data_2, ram_1_data}), .in1(bit_extender_1_out),
    .in2({{16{1'b0}}, multiplexer_4_out}), .in3(bit_extender_2_out), .in4({{24{1'b0}}, multiplexer_5_out}),
    .in5({32{1'b0}}), .in6({32{1'b0}}), .in7({32{1'b0}}), .out(RD), .sel(Load));
endmodule

module ExtU (
  input  [1:0] ExtOP,
  input  [15:0] ImmIn,
  output [31:0] ImmOut
);

  wire [31:0] bit_extender_1_out, bit_extender_2_out, bit_extender_3_out, shifter_1_out;

  assign bit_extender_1_out = {{16{1'b0}}, ImmIn};  // Bit_Extender bit_extender_1
  assign bit_extender_2_out = {{16{ImmIn[15]}}, ImmIn};  // Bit_Extender bit_extender_2
  assign bit_extender_3_out = {{16{1'b0}}, ImmIn};  // Bit_Extender bit_extender_3
  Shifter #(.width(32)) shifter_1 (.in(bit_extender_3_out), .\dist (5'b10000), .out(shifter_1_out));
  Multiplexer #(.select(2), .width(32)) multiplexer_1 (
    .in0(bit_extender_1_out), .in1(bit_extender_2_out), .in2(shifter_1_out), .out(ImmOut), .sel(ExtOP));  // open: in3, en
endmodule

module ControlUnit (
  input  Op5,
  input  Op4,
  input  Op3,
  input  Op2,
  input  Op1,
  input  Op0,
  input  Funct5,
  input  Funct4,
  input  Funct3,
  input  Funct2,
  input  Funct1,
  input  Funct0,
  output Jarl,
  output RegWriteEN,
  output RegDst1,
  output RegDst0,
  output ExtOp1,
  output ExtOp0,
  output ALUSrc_SrcB,
  output ALUCtrl3,
  output ALUCtrl2,
  output ALUCtrl1,
  output ALUCtrl0,
  output Branch2,
  output Branch1,
  output Branch0,
  output MenWrite,
  output Men2Reg,
  output J_Type,
  output J_Jal,
  output Load2,
  output Load1,
  output Load0
);

  wire addiu_out, addu_out, and_out, andi_out, beq_out, bgez_out, bgtz_out, blez_out, bltz_out, bne_out,
       j_out, jal_out, jr_out, lb_out, lbu_out, lh_out, lhu_out, lui_out, lw_out, nor_out, not_1_out,
       not_2_out, not_3_out, not_4_out, not_5_out, not_6_out, not_7_out, not_8_out, not_9_out, not_10_out,
       not_11_out, not_12_out, or_out, ori_out, sb_out, sh_out, sll_out, sllv_out, slt_out, slti_out,
       sltiu_out, sltu_out, sra_out, srav_out, srl_out, srlv_out, subu_out, sw_out, xor_out, xori_out;

  not not_1 (not_1_out, Op5);
  not not_2 (not_2_out, Op3);
  not not_3 (not_3_out, Op4);
  not not_4 (not_4_out, Op2);
  not not_5 (not_5_out, Op1);
  not not_6 (not_6_out, Funct5);
  not not_7 (not_7_out, Op0);
  not not_8 (not_8_out, Funct3);
  not not_9 (not_9_out, Funct4);
  not not_10 (not_10_out, Funct2);
  not not_11 (not_11_out, Funct1);
  not not_12 (not_12_out, Funct0);
  and addu (addu_out, not_7_out, not_5_out, not_4_out, not_2_out, not_3_out, not_1_out, Funct0, not_11_out, not_10_out, not_8_out, not_9_out, Funct5);
  and subu (subu_out, not_7_out, not_5_out, not_4_out, not_2_out, not_3_out, not_1_out, Funct0, Funct1, not_10_out, not_8_out, not_9_out, Funct5);
  and ori (ori_out, Op0, not_5_out, Op2, Op3, not_3_out, not_1_out);
  and lw (lw_out, Op0, Op1, not_4_out, not_2_out, not_3_out, Op5);
  and sw (sw_out, Op0, Op1, not_4_out, Op3, not_3_out, Op5);
  and beq (beq_out, not_7_out, not_5_out, Op2, not_2_out, not_3_out, not_1_out);
  and lui (lui_out, Op0, Op1, Op2, Op3, not_3_out, not_1_out);
  and sh (sh_out, Op0, not_5_out, not_4_out, Op3, not_3_out, Op5);
  and jal (jal_out, not_1_out, not_3_out, not_2_out, not_4_out, Op1, Op0);
  and jr (jr_out, not_7_out, not_5_out, not_4_out, not_2_out, not_3_out, not_1_out, not_12_out, not_11_out, not_10_out, Funct3, not_9_out, not_6_out);
  and lh (lh_out, Op0, not_5_out, not_4_out, not_2_out, not_3_out, Op5);
  and lhu (lhu_out, Op5, not_3_out, not_2_out, Op2, not_5_out, Op0);
  and lb (lb_out, Op5, not_3_out, not_2_out, not_4_out, not_5_out, not_7_out);
  and lbu (lbu_out, Op5, not_3_out, not_2_out, Op2, not_5_out, not_7_out);
  and sb (sb_out, Op5, not_3_out, Op3, not_4_out, not_5_out, not_7_out);
  and addiu (addiu_out, not_1_out, not_3_out, Op3, not_4_out, not_5_out, Op0);
  and \and  (and_out, not_7_out, not_5_out, not_4_out, not_2_out, not_3_out, not_1_out, Funct5, not_9_out, not_8_out, Funct2, not_11_out, not_12_out);
  and andi (andi_out, not_1_out, not_3_out, Op3, Op2, not_5_out, not_7_out);
  and \nor  (nor_out, not_7_out, not_5_out, not_4_out, not_2_out, not_3_out, not_1_out, Funct5, not_9_out, not_8_out, Funct2, Funct1, Funct0);
  and \or  (or_out, not_7_out, not_5_out, not_4_out, not_2_out, not_3_out, not_1_out, Funct5, not_9_out, not_8_out, Funct2, not_11_out, Funct0);
  and \xor  (xor_out, not_7_out, not_5_out, not_4_out, not_2_out, not_3_out, not_1_out, Funct5, not_9_out, not_8_out, Funct2, Funct1, not_12_out);
  and xori (xori_out, not_1_out, not_3_out, Op3, Op2, Op1, not_7_out);
  and j (j_out, not_1_out, not_3_out, not_2_out, not_4_out, Op1, not_7_out);
  and jalr (Jarl, not_7_out, not_5_out, not_4_out, not_2_out, not_3_out, not_1_out, not_6_out, not_9_out, Funct3, not_10_out, not_11_out, Funct0);
  and bgez (bgez_out, not_1_out, not_3_out, not_2_out, not_4_out, not_5_out, Op0, not_6_out, not_9_out, not_8_out, not_10_out, not_11_out, Funct0);
  and bltz (bltz_out, not_1_out, not_3_out, not_2_out, not_4_out, not_5_out, Op0, not_6_out, not_9_out, not_8_out, not_10_out, not_11_out, not_12_out);
  and bgtz (bgtz_out, not_1_out, not_3_out, not_2_out, Op2, Op1, Op0);
  and blez (blez_out, not_1_out, not_3_out, not_2_out, Op2, Op1, not_7_out);
  and bne (bne_out, not_1_out, not_3_out, not_2_out, Op2, not_5_out, Op0);
  and slt (slt_out, not_1_out, not_3_out, not_2_out, not_4_out, not_5_out, not_7_out, Funct5, not_9_out, Funct3, not_10_out, Funct1, not_12_out);
  and slti (slti_out, not_1_out, not_3_out, Op3, not_4_out, Op1, not_7_out);
  and sltiu (sltiu_out, not_1_out, not_3_out, Op3, not_4_out, Op1, Op0);
  and sltu (sltu_out, not_1_out, not_3_out, not_2_out, not_4_out, not_5_out, not_7_out, Funct5, not_9_out, Funct3, not_10_out, Funct1, Funct0);
  and sll (sll_out, not_1_out, not_3_out, not_2_out, not_4_out, not_5_out, not_7_out, not_6_out, not_9_out, not_8_out, not_10_out, not_11_out, not_12_out);
  and sllv (sllv_out, not_1_out, not_3_out, not_2_out, not_4_out, not_5_out, not_7_out, not_6_out, not_9_out, not_8_out, Funct2, not_11_out, not_12_out);
  and sra (sra_out, not_1_out, not_3_out, not_2_out, not_4_out, not_5_out, not_7_out, not_6_out, not_9_out, not_8_out, not_10_out, Funct1, Funct0);
  and srav (srav_out, not_1_out, not_3_out, not_2_out, not_4_out, not_5_out, not_7_out, not_6_out, not_9_out, not_8_out, Funct2, Funct1, Funct0);
  and srl (srl_out, not_1_out, not_3_out, not_2_out, not_4_out, not_5_out, not_7_out, not_6_out, not_9_out, not_8_out, not_10_out, Funct1, not_12_out);
  and srlv (srlv_out, not_1_out, not_3_out, not_2_out, not_4_out, not_5_out, not_7_out, not_6_out, not_9_out, not_8_out, Funct2, Funct1, not_12_out);
  or or_2 (RegWriteEN, jal_out, lui_out, addu_out, subu_out, ori_out, lw_out, lh_out, lhu_out, lb_out, lbu_out, addiu_out, and_out, andi_out, nor_out, or_out, xor_out, xori_out, Jarl, slt_out, slti_out, sltiu_out, sltu_out, sll_out, sllv_out, sra_out, srav_out, srl_out, srlv_out);
  buf or_3 (RegDst1, jal_out);  // OR_Gate
  or or_4 (RegDst0, addu_out, subu_out, and_out, nor_out, or_out, xor_out, Jarl, slt_out, sll_out, sllv_out, sra_out, srav_out, srl_out, srlv_out, sltu_out);
  buf or_5 (ExtOp1, lui_out);  // OR_Gate
  or or_6 (ExtOp0, lw_out, sw_out, beq_out, sh_out, lh_out, lhu_out, lb_out, lbu_out, sb_out, addiu_out, slti_out, sltiu_out);
  or or_7 (ALUSrc_SrcB, ori_out, lw_out, sw_out, sh_out, lui_out, lh_out, lhu_out, lb_out, lbu_out, sb_out, addiu_out, xori_out, slti_out, sltiu_out, andi_out);
  or or_8 (ALUCtrl3, sra_out, sll_out, sllv_out, srav_out, srl_out, srlv_out);
  or or_9 (ALUCtrl2, srlv_out, srl_out, sltu_out, sltiu_out, nor_out, xor_out, xori_out, slt_out, slti_out);
  or or_10 (ALUCtrl1, ori_out, and_out, andi_out, or_out, slt_out, slti_out, sltiu_out, sltu_out, sra_out, srav_out);
  or or_11 (ALUCtrl0, subu_out, beq_out, and_out, andi_out, xor_out, xori_out, sltiu_out, sltu_out, sllv_out, srav_out, srlv_out, bne_out);
  or or_12 (Branch2, bltz_out, blez_out, bne_out);
  or or_13 (Branch1, bgez_out, bgtz_out, bne_out);
  or or_14 (Branch0, beq_out, bltz_out, bgtz_out);
  or or_15 (MenWrite, sw_out, sh_out, sb_out);
  or or_16 (Men2Reg, lw_out, lh_out, lhu_out, lb_out, lbu_out);
  or or_17 (J_Type, jr_out, jal_out, j_out, Jarl);
  or or_18 (J_Jal, jal_out, j_out);
  or or_19 (Load1, sb_out, lb_out, lhu_out);
  buf or_20 (Load2, lbu_out);  // OR_Gate
  or or_21 (Load0, lh_out, sh_out, lb_out);
endmodule
