// Logisim project [p3]SingleCycleCPU-at20171121-0223.circ as structural Verilog
module main (
  input  Reset
);

  wire Clk;
  wire [31:0] alu_1_aluresult, dm_1_rd, grf_1_rd1, grf_1_rd1_2, ifu_1_instruction, ifu_1_signedimmediate,
       multiplexer_1_out, multiplexer_2_out;

  Clock clock_1 (.out(Clk));
  IFU ifu_1 (
    .Instruction(ifu_1_instruction), .Reset(Reset), .SignedImmediate(ifu_1_signedimmediate), .Clk(Clk));  // open: PCSrc
  ControlUnit controlunit_1 ();
  GRF grf_1 (
    .Clk(Clk), .A1_25_21__rs(ifu_1_instruction[25:21]), .A2_20_16__rt(ifu_1_instruction[20:16]),
    ._15_11(ifu_1_instruction[15:11]), .WD3(multiplexer_2_out), .Reset(Reset), .RD1(grf_1_rd1),
    .RD1_2(grf_1_rd1_2));  // open: WE, RegDst_A3
  Multiplexer #(.width(32), .enable("false")) multiplexer_1 (
    .in0(grf_1_rd1_2), .in1(ifu_1_signedimmediate), .out(multiplexer_1_out));  // open: sel
  ALU alu_1 (
    .SrcA(grf_1_rd1), .SrcB(multiplexer_1_out), .ALUResult(alu_1_aluresult));  // open: Zero_beq_SrcA__SrcB_1_0, ALUCtrl
  DM dm_1 (.ALUResult_Addr(alu_1_aluresult), .RD2_WD(grf_1_rd1_2), .RD(dm_1_rd), .Clk(Clk), .Reset(Reset));  // open: WE
  Multiplexer #(.width(32), .enable("false")) multiplexer_2 (
    .in0(alu_1_aluresult), .in1(dm_1_rd), .out(multiplexer_2_out));  // open: sel
endmodule

module IFU (
  input  PCSrc,
  input  Reset,
  input  Clk,
  output [31:0] Instruction,
  output [31:0] SignedImmediate
);

  wire [31:0] adder_1_out, bit_extender_1_out, multiplexer_1_out, PC_q;

  Multiplexer #(.width(32), .enable("false")) multiplexer_1 (
    .in0(adder_1_out), .in1(SignedImmediate), .out(multiplexer_1_out), .sel(PCSrc));
  Register #(.width(32)) PC (.D(multiplexer_1_out), .Q(PC_q), .clk(Clk), .clr(Reset));  // open: en
  Adder #(.width(32)) adder_1 (.a(PC_q), .b(32'h1), .out(adder_1_out));  // open: cin, cout
  ROM #(.addrWidth(5), .dataWidth(32)) rom_1 (.addr(PC_q[4:0]), .data(Instruction));  // open: sel
  assign bit_extender_1_out = {{16{Instruction[15]}}, Instruction[15:0]};  // Bit_Extender bit_extender_1
  Adder #(.width(32)) adder_2 (.a(bit_extender_1_out), .b(adder_1_out), .out(SignedImmediate));  // open: cin, cout

  // Notes on the sheet:
  //   contents of rom_1 (hex, n*v repeats v):
  //   233 2333 23333 342 6747 dd bb cc ee
endmodule

module GRF (
  input  Clk,
  input  WE,
  input  [4:0] A1_25_21__rs,
  input  [4:0] A2_20_16__rt,
  input  [4:0] _15_11,
  input  [31:0] WD3,
  input  RegDst_A3,
  input  Reset,
  output [31:0] RD1,
  output [31:0] RD1_2
);

  wire and_1_out, and_2_out, and_3_out, and_4_out, and_5_out, and_6_out, and_7_out, and_8_out, and_9_out,
       and_10_out, and_11_out, and_12_out, and_13_out, and_14_out, and_15_out, and_16_out, and_17_out,
       and_18_out, and_19_out, and_20_out, and_21_out, and_22_out, and_23_out, and_24_out, and_25_out,
       and_26_out, and_27_out, and_28_out, and_29_out, and_30_out, and_31_out, w1, w2, w3, w4, w5, w6, w7,
       w8, w9, w10, w11, w12, w13, w14, w15, w16, w17, w18, w19, w20, w21, w22, w23, w24, w25, w26, w27, w28,
       w29, w30, w31;
  wire [4:0] multiplexer_1_out;
  wire [31:0] rd_1, rd_2, rd_3, rd_4, rd_5, rd_6, rd_7, rd_8, rd_9, rd_10, rd_11, rd_12, rd_13, rd_14, rd_15,
       rd_16, rd_17, rd_18, rd_19, rd_20, rd_21, rd_22, rd_23, rd_24, rd_25, rd_26, rd_27, rd_28, rd_29,
       rd_30, rd_31;

  Register #(.width(32)) _8 (.D(WD3), .en(and_1_out), .Q(rd_8), .clk(Clk), .clr(Reset));
  and and_1 (and_1_out, w8, WE);
  Register #(.width(32)) _16 (.D(WD3), .en(and_2_out), .Q(rd_16), .clk(Clk), .clr(Reset));
  and and_2 (and_2_out, w16, WE);
  Register #(.width(32)) _24 (.D(WD3), .en(and_3_out), .Q(rd_24), .clk(Clk), .clr(Reset));
  and and_3 (and_3_out, w24, WE);
  Multiplexer #(.width(5), .enable("false")) multiplexer_1 (
    .in0(A2_20_16__rt), .in1(_15_11), .out(multiplexer_1_out), .sel(RegDst_A3));
  and and_4 (and_4_out, w1, WE);
  and and_5 (and_5_out, w9, WE);
  and and_6 (and_6_out, w17, WE);
  and and_7 (and_7_out, w25, WE);
  Decoder #(.select(5), .enable("false")) decoder_1 (
    .out1(w1), .out2(w2), .out3(w3), .out4(w4), .out5(w5), .out6(w6), .out7(w7), .out8(w8), .out9(w9),
    .out10(w10), .out11(w11), .out12(w12), .out13(w13), .out14(w14), .out15(w15), .out16(w16), .out17(w17),
    .out18(w18), .out19(w19), .out20(w20), .out21(w21), .out22(w22), .out23(w23), .out24(w24), .out25(w25),
    .out26(w26), .out27(w27), .out28(w28), .out29(w29), .out30(w30), .out31(w31), .sel(multiplexer_1_out));  // open: out0
  Register #(.width(32)) _1 (.D(WD3), .en(and_4_out), .Q(rd_1), .clk(Clk), .clr(Reset));
  Register #(.width(32)) _9 (.D(WD3), .en(and_5_out), .Q(rd_9), .clk(Clk), .clr(Reset));
  Register #(.width(32)) _17 (.D(WD3), .en(and_6_out), .Q(rd_17), .clk(Clk), .clr(Reset));
  Register #(.width(32)) _25 (.D(WD3), .en(and_7_out), .Q(rd_25), .clk(Clk), .clr(Reset));
  and and_8 (and_8_out, w2, WE);
  and and_9 (and_9_out, w10, WE);
  and and_10 (and_10_out, w18, WE);
  and and_11 (and_11_out, w26, WE);
  Register #(.width(32)) _2 (.D(WD3), .en(and_8_out), .Q(rd_2), .clk(Clk), .clr(Reset));
  Register #(.width(32)) _10 (.D(WD3), .en(and_9_out), .Q(rd_10), .clk(Clk), .clr(Reset));
  Register #(.width(32)) _18 (.D(WD3), .en(and_10_out), .Q(rd_18), .clk(Clk), .clr(Reset));
  Register #(.width(32)) _26 (.D(WD3), .en(and_11_out), .Q(rd_26), .clk(Clk), .clr(Reset));
  and and_12 (and_12_out, w3, WE);
  and and_13 (and_13_out, w11, WE);
  and and_14 (and_14_out, w19, WE);
  and and_15 (and_15_out, w27, WE);
  Register #(.width(32)) _3 (.D(WD3), .en(and_12_out), .Q(rd_3), .clk(Clk), .clr(Reset));
  Register #(.width(32)) _11 (.D(WD3), .en(and_13_out), .Q(rd_11), .clk(Clk), .clr(Reset));
  Register #(.width(32)) _19 (.D(WD3), .en(and_14_out), .Q(rd_19), .clk(Clk), .clr(Reset));
  Register #(.width(32)) _27 (.D(WD3), .en(and_15_out), .Q(rd_27), .clk(Clk), .clr(Reset));
  and and_16 (and_16_out, w4, WE);
  and and_17 (and_17_out, w12, WE);
  and and_18 (and_18_out, w20, WE);
  and and_19 (and_19_out, w28, WE);
  Register #(.width(32)) _4 (.D(WD3), .en(and_16_out), .Q(rd_4), .clk(Clk), .clr(Reset));
  Register #(.width(32)) _12 (.D(WD3), .en(and_17_out), .Q(rd_12), .clk(Clk), .clr(Reset));
  Register #(.width(32)) _20 (.D(WD3), .en(and_18_out), .Q(rd_20), .clk(Clk), .clr(Reset));
  Register #(.width(32)) _28 (.D(WD3), .en(and_19_out), .Q(rd_28), .clk(Clk), .clr(Reset));
  Register #(.width(32)) _5 (.D(WD3), .en(and_20_out), .Q(rd_5), .clk(Clk), .clr(Reset));
  and and_20 (and_20_out, w5, WE);
  Register #(.width(32)) _13 (.D(WD3), .en(and_21_out), .Q(rd_13), .clk(Clk), .clr(Reset));
  and and_21 (and_21_out, w13, WE);
  Register #(.width(32)) _21 (.D(WD3), .en(and_22_out), .Q(rd_21), .clk(Clk), .clr(Reset));
  and and_22 (and_22_out, w21, WE);
  Register #(.width(32)) _29 (.D(WD3), .en(and_23_out), .Q(rd_29), .clk(Clk), .clr(Reset));
  and and_23 (and_23_out, w29, WE);
  Register #(.width(32)) _6 (.D(WD3), .en(and_24_out), .Q(rd_6), .clk(Clk), .clr(Reset));
  and and_24 (and_24_out, w6, WE);
  Register #(.width(32)) _14 (.D(WD3), .en(and_25_out), .Q(rd_14), .clk(Clk), .clr(Reset));
  and and_25 (and_25_out, w14, WE);
  Register #(.width(32)) _22 (.D(WD3), .en(and_26_out), .Q(rd_22), .clk(Clk), .clr(Reset));
  and and_26 (and_26_out, w22, WE);
  Register #(.width(32)) _30 (.D(WD3), .en(and_27_out), .Q(rd_30), .clk(Clk), .clr(Reset));
  and and_27 (and_27_out, w30, WE);
  Register #(.width(32)) _7 (.D(WD3), .en(and_28_out), .Q(rd_7), .clk(Clk), .clr(Reset));
  and and_28 (and_28_out, w7, WE);
  Register #(.width(32)) _15 (.D(WD3), .en(and_29_out), .Q(rd_15), .clk(Clk), .clr(Reset));
  and and_29 (and_29_out, w15, WE);
  Register #(.width(32)) _23 (.D(WD3), .en(and_30_out), .Q(rd_23), .clk(Clk), .clr(Reset));
  and and_30 (and_30_out, w23, WE);
  Register #(.width(32)) _31 (.D(WD3), .en(and_31_out), .Q(rd_31), .clk(Clk), .clr(Reset));
  and and_31 (and_31_out, w31, WE);
  Multiplexer #(.select(5), .width(32), .enable("false")) multiplexer_2 (
    .in0({32{1'b0}}), .in1(rd_1), .in2(rd_2), .in3(rd_3), .in4(rd_4), .in5(rd_5), .in6(rd_6), .in7(rd_7),
    .in8(rd_8), .in9(rd_9), .in10(rd_10), .in11(rd_11), .in12(rd_12), .in13(rd_13), .in14(rd_14),
    .in15(rd_15), .in16(rd_16), .in17(rd_17), .in18(rd_18), .in19(rd_19), .in20(rd_20), .in21(rd_21),
    .in22(rd_22), .in23(rd_23), .in24(rd_24), .in25(rd_25), .in26(rd_26), .in27(rd_27), .in28(rd_28),
    .in29(rd_29), .in30(rd_30), .in31(rd_31), .out(RD1), .sel(A1_25_21__rs));
  Multiplexer #(.select(5), .width(32), .enable("false")) multiplexer_3 (
    .in0({32{1'b0}}), .in1(rd_1), .in2(rd_2), .in3(rd_3), .in4(rd_4), .in5(rd_5), .in6(rd_6), .in7(rd_7),
    .in8(rd_8), .in9(rd_9), .in10(rd_10), .in11(rd_11), .in12(rd_12), .in13(rd_13), .in14(rd_14),
    .in15(rd_15), .in16(rd_16), .in17(rd_17), .in18(rd_18), .in19(rd_19), .in20(rd_20), .in21(rd_21),
    .in22(rd_22), .in23(rd_23), .in24(rd_24), .in25(rd_25), .in26(rd_26), .in27(rd_27), .in28(rd_28),
    .in29(rd_29), .in30(rd_30), .in31(rd_31), .out(RD1_2));  // open: sel

  // Other names for the same wires on the sheet: A1[4:0] = A1_25_21__rs
endmodule

module ALU (
  input  [3:0] ALUCtrl,
  input  [31:0] SrcA,
  input  [31:0] SrcB,
  output Zero_beq_SrcA__SrcB_1_0,
  output [31:0] ALUResult
);

  wire [31:0] adder_1_out, and_1_out, or_1_out, subtractor_1_out;

  Adder #(.width(32)) adder_1 (.a(SrcA), .b(SrcB), .out(adder_1_out));  // open: cin, cout
  Subtractor #(.width(32)) subtractor_1 (.a(SrcA), .b(SrcB), .out(subtractor_1_out));  // open: bin, bout
  assign or_1_out = SrcA | SrcB;  // OR_Gate or_1, 32 bits wide
  assign and_1_out = SrcA & SrcB;  // AND_Gate and_1, 32 bits wide
  Multiplexer #(.select(4), .width(32), .enable("false")) multiplexer_1 (
    .in0(adder_1_out), .in1(subtractor_1_out), .in2(or_1_out), .out(ALUResult), .sel(ALUCtrl));  // open: in3, in4, in5, in6, in7, in8, in9, in10, in11, in12, in13, in14, in15
  Comparator #(.width(32), .mode("unsigned")) comparator_1 (
    .a({32{1'b0}}), .b(ALUResult), .eq(Zero_beq_SrcA__SrcB_1_0));  // open: gt, lt
endmodule

module DM (
  input  [31:0] ALUResult_Addr,
  input  WE,
  input  Clk,
  input  Reset,
  input  [31:0] RD2_WD,
  output [31:0] RD
);

  RAM #(.addrWidth(5), .dataWidth(32), .bus("separate")) ram_1 (
    .addr(ALUResult_Addr[4:0]), .din(RD2_WD), .data(RD), .str(WE), .clk(Clk), .ld(1'b1), .clr(Reset));  // open: sel
endmodule
