// Logisim project [王端瑞]p0_1.circ as structural Verilog: 3 circuits, main circuit 4bit
module _4bit (
  input  in_1,
  input  in_2,
  input  in_3,
  input  in_4,
  input  in_5,
  input  in_6,
  input  in_7,
  output d,
  output out_9,
  output out_10,
  output out_11
);

  wire and_1_out, and_2_out, and_3_out, and_4_out, and_5_out, and_6_out, not_1_out, xor_1_out, xor_2_out,
       xor_3_out;

  not not_1 (not_1_out, in_1);
  xor xor_1 (xor_1_out, in_2, in_5);
  xor xor_2 (xor_2_out, in_3, in_6);
  xor xor_3 (xor_3_out, in_4, in_7);
  and and_1 (and_1_out, in_1, xor_1_out);
  and and_2 (and_2_out, in_2, not_1_out);
  and and_3 (and_3_out, in_1, xor_2_out);
  and and_4 (and_4_out, not_1_out, in_3);
  and and_5 (and_5_out, in_1, xor_3_out);
  and and_6 (and_6_out, not_1_out, in_4);
  or or_1 (out_9, and_1_out, and_2_out);
  or or_2 (out_10, and_3_out, and_4_out);
  or or_3 (out_11, and_5_out, and_6_out);

  assign d = in_1;
endmodule

module CRC (
  input  [7:0] in_1,
  input  [3:0] in_2,
  output [10:0] out_3
);

  wire n4bit_1_out_9, n4bit_1_out_10, n4bit_1_out_11, n4bit_2_out_9, n4bit_2_out_10, n4bit_2_out_11,
       n4bit_3_out_9, n4bit_3_out_10, n4bit_3_out_11, n4bit_4_out_9, n4bit_4_out_10, n4bit_4_out_11;

  _4bit u_4bit_1 (
    .in_1(in_1[0]), .in_2(in_1[1]), .in_3(in_1[2]), .in_4(in_1[3]), .in_5(in_2[1]), .in_6(in_2[2]),
    .in_7(in_2[3]), .out_9(n4bit_1_out_9), .out_10(n4bit_1_out_10), .out_11(n4bit_1_out_11));  // open: d
  _4bit u_4bit_2 (
    .in_1(n4bit_1_out_9), .in_2(n4bit_1_out_10), .in_3(n4bit_1_out_11), .in_4(in_1[4]), .in_5(in_2[1]),
    .in_6(in_2[2]), .in_7(in_2[3]), .out_9(n4bit_2_out_9), .out_10(n4bit_2_out_10), .out_11(n4bit_2_out_11));  // open: d
  _4bit u_4bit_3 (
    .in_1(n4bit_2_out_9), .in_2(n4bit_2_out_10), .in_3(n4bit_2_out_11), .in_4(in_1[5]), .in_5(in_2[1]),
    .in_6(in_2[2]), .in_7(in_2[3]), .out_9(n4bit_3_out_9), .out_10(n4bit_3_out_10), .out_11(n4bit_3_out_11));  // open: d
  _4bit u_4bit_4 (
    .in_1(n4bit_3_out_9), .in_2(n4bit_3_out_10), .in_3(n4bit_3_out_11), .in_4(in_1[6]), .in_5(in_2[1]),
    .in_6(in_2[2]), .in_7(in_2[3]), .out_9(n4bit_4_out_9), .out_10(n4bit_4_out_10), .out_11(n4bit_4_out_11));  // open: d
  _4bit u_4bit_5 (
    .in_1(n4bit_4_out_9), .in_2(n4bit_4_out_10), .in_3(n4bit_4_out_11), .in_4(in_1[7]), .in_5(in_2[1]),
    .in_6(in_2[2]), .in_7(in_2[3]), .out_9(out_3[8]), .out_10(out_3[9]), .out_11(out_3[10]));  // open: d

  assign out_3[7:0] = in_1;
endmodule

module check (
  output [10:0] out_1,
  output out_2
);

  wire clock_1_out;
  wire [3:0] counter_1_q;
  wire [11:0] rom_1_data;

  Counter #(.width(4), .max('hf)) counter_1 (
    .Q(counter_1_q), .carry(out_2), .clk(clock_1_out));  // open: load, D, count, clr
  Clock clock_1 (.out(clock_1_out));
  ROM #(.addrWidth(4), .dataWidth(12)) rom_1 (.addr(counter_1_q), .data(rom_1_data));  // open: sel
  CRC crc_1 (.in_1(rom_1_data[7:0]), .in_2(rom_1_data[11:8]), .out_3(out_1));

  // Notes on the sheet:
  //   contents of rom_1 (hex, n*v repeats v):
  //   0 0 1
endmodule
