// Logisim project [王端瑞]p0_3.circ as structural Verilog: 4 circuits, main circuit fsm
module fsm (
  input  in_1,
  input  [1:0] in_2,
  output out_3
);

  wire and_1_out, clock_1_out, register_1_q;
  wire [1:0] move_1_next, register_2_q;

  Register #(.width(1)) register_1 (.D(in_1), .Q(register_1_q), .clk(clock_1_out));  // open: en, clr
  // Probe on register_2_q
  // Probe on move_1_next
  move move_1 (.current(register_2_q), .\input (in_2), .next(move_1_next));
  and and_1 (and_1_out, in_1, register_1_q);
  Register #(.width(2)) register_2 (.D(move_1_next), .Q(register_2_q), .clk(clock_1_out), .clr(and_1_out));  // open: en
  Clock clock_1 (.out(clock_1_out));
  // Probe on register_2_q
  out out_1 (.s(in_2), .\input (register_2_q), .out_3(out_3));
endmodule

module move (
  input  [1:0] current,
  input  [1:0] \input ,
  output [1:0] next
);

  wire and_1_out, and_2_out, and_3_out, and_4_out, not_1_out, not_2_out, not_3_out, not_4_out;

  not not_1 (not_1_out, current[0]);
  not not_2 (not_2_out, current[1]);
  not not_3 (not_3_out, \input [0]);
  not not_4 (not_4_out, \input [1]);
  and and_1 (and_1_out, not_3_out, current[0], not_2_out);
  and and_2 (and_2_out, current[1], not_3_out, not_1_out);
  and and_3 (and_3_out, not_4_out, \input [0]);
  and and_4 (and_4_out, not_1_out, current[1], not_3_out);
  or or_1 (next[1], and_1_out, and_2_out);
  or or_2 (next[0], and_3_out, and_4_out);
endmodule

module out (
  input  [1:0] s,
  input  [1:0] \input ,
  output out_3
);

  wire not_1_out, not_2_out;

  not not_1 (not_1_out, s[0]);
  not not_2 (not_2_out, \input [0]);
  and and_1 (out_3, not_1_out, not_2_out, \input [1]);
endmodule

module move2 (
  input  [1:0] current,
  input  [1:0] \input ,
  output next
);
endmodule
