// Logisim project selectFibNum.circ as structural Verilog: 1 circuit, main circuit main
module main (
  input  [2:0] in_1,
  output [3:0] out_2
);

  Multiplexer #(.select(3), .width(4), .enable("false")) multiplexer_1 (
    .in0(4'b0000), .in1(4'b0001), .in2(4'b0001), .in3(4'b0010), .in4(4'b0011), .in5(4'b0101), .in6(4'b1000),
    .in7(4'b1101), .out(out_2), .sel(in_1));
endmodule
