// Logisim project test！！.circ as structural Verilog: 1 circuit, main circuit main
module main (
  output out_1,
  output [1:0] out_2
);

  wire clock_1_out, counter_1_carry;
  wire [1:0] bit_extender_1_out;
  wire [2:1] rom_1_data;
  wire [7:0] counter_1_q;

  Counter counter_1 (.Q(counter_1_q), .carry(counter_1_carry), .clk(clock_1_out));  // open: load, D, count, clr
  Clock clock_1 (.out(clock_1_out));
  ROM #(.dataWidth(3)) rom_1 (.addr(counter_1_q), .data({rom_1_data, out_1}));  // open: sel
  // Probe on rom_1_data
  assign bit_extender_1_out = {{1{1'b0}}, out_1};  // Bit_Extender bit_extender_1
  assign out_2 = bit_extender_1_out & rom_1_data;  // AND_Gate and_1, 2 bits wide
endmodule
