// Logisim project 【丁振辉】fast exponentiation.circ as structural Verilog: 2 circuits, main circuit main
module main (
  input  [7:0] in_1,
  input  [7:0] in_2
);

  wire clock_1_out, comparator_1_eq, not_1_out;
  wire [7:0] initialized_register_1_q, initialized_register_2_q, initialized_register_3_q, multiplier_1_out,
       multiplier_2_out, shifter_1_out;

  initialized_register initialized_register_1 (
    .ini(in_2), .Data(shifter_1_out), .Enable(not_1_out), .Clk(clock_1_out), .Q(initialized_register_1_q));
  Comparator comparator_1 (.a(initialized_register_1_q), .b({8{1'b0}}), .eq(comparator_1_eq));  // open: gt, lt
  not not_1 (not_1_out, comparator_1_eq);
  Shifter #(.shift("lr")) shifter_1 (.in(initialized_register_1_q), .\dist (3'b001), .out(shifter_1_out));
  initialized_register initialized_register_2 (
    .ini(in_1), .Data(multiplier_1_out), .Enable(not_1_out), .Clk(clock_1_out), .Q(initialized_register_2_q));
  initialized_register initialized_register_3 (
    .ini(8'h1), .Data(multiplier_2_out), .Enable(initialized_register_1_q[0]), .Clk(clock_1_out),
    .Q(initialized_register_3_q));
  Clock clock_1 (.out(clock_1_out));
  // Probe on initialized_register_3_q
  Multiplier multiplier_1 (
    .a(initialized_register_2_q), .b(initialized_register_2_q), .out(multiplier_1_out));  // open: cin, cout
  Multiplier multiplier_2 (
    .a(initialized_register_2_q), .b(initialized_register_3_q), .out(multiplier_2_out));  // open: cin, cout
endmodule

module initialized_register (
  input  [7:0] ini,
  input  [7:0] Data,
  input  Enable,
  input  Clk,
  output [7:0] Q
);

  wire clock_1_out, clock_2_out, comparator_1_eq, multiplexer_2_out, register_1_q;
  wire [1:0] counter_1_q;
  wire [7:0] multiplexer_1_out;

  Clock clock_1 (.out(clock_1_out));
  Counter #(.width(2), .max('h3), .ongoal("stay")) counter_1 (
    .Q(counter_1_q), .clk(clock_1_out));  // open: load, D, count, carry, clr
  Register #(.width(1)) register_1 (.D(1'b1), .Q(register_1_q), .clk(clock_2_out));  // open: en, clr
  Clock clock_2 (.out(clock_2_out));
  Comparator #(.width(2), .mode("unsigned")) comparator_1 (
    .a(counter_1_q), .b(2'b01), .eq(comparator_1_eq));  // open: gt, lt
  Multiplexer #(.width(8), .enable("false")) multiplexer_1 (
    .in0(ini), .in1(Data), .out(multiplexer_1_out), .sel(register_1_q));
  Multiplexer #(.enable("false")) multiplexer_2 (.in0(1'b1), .in1(Enable), .out(multiplexer_2_out), .sel(register_1_q));
  Register register_2 (.D(multiplexer_1_out), .en(multiplexer_2_out), .Q(Q), .clk(Clk));  // open: clr
endmodule
