// Logisim project 【丁振辉】fibonacci(fast matrix exponentiation).circ as structural Verilog: 4 circuits, main circuit main
module main (
  input  [31:0] in_1,
  output [31:0] out_2
);

  wire bit_extender_1_out, clock_1_out, comparator_1_eq, not_1_out;
  wire [31:0] initialized_register_1_q, matrix_multiplier_1_c11, matrix_multiplier_1_c12,
       matrix_multiplier_1_c21, matrix_multiplier_1_c22, matrix_multiplier_2_c11, matrix_multiplier_2_c12,
       matrix_multiplier_2_c21, matrix_multiplier_2_c22, n2_by_2_matrix_1_out_11, n2_by_2_matrix_1_out_12,
       n2_by_2_matrix_1_out_13, n2_by_2_matrix_1_out_14, n2_by_2_matrix_2_out_11, n2_by_2_matrix_2_out_12,
       n2_by_2_matrix_2_out_13, n2_by_2_matrix_2_out_14, shifter_1_out;

  initialized_register initialized_register_1 (
    .ini(in_1), .Data(shifter_1_out), .Enable(not_1_out), .CLK(clock_1_out), .Q(initialized_register_1_q));
  Comparator #(.width(32), .mode("unsigned")) comparator_1 (
    .a(initialized_register_1_q), .b({32{1'b0}}), .eq(comparator_1_eq));  // open: gt, lt
  Bit_Extender #(.in_width(32), .out_width(1)) bit_extender_1 (.in(initialized_register_1_q), .out(bit_extender_1_out));
  Shifter #(.width(32), .shift("lr")) shifter_1 (.in(initialized_register_1_q), .\dist (5'b00001), .out(shifter_1_out));
  not not_1 (not_1_out, comparator_1_eq);
  Clock clock_1 (.out(clock_1_out));
  _2_by_2_matrix u_2_by_2_matrix_1 (
    .a11(matrix_multiplier_1_c11), .a12(matrix_multiplier_1_c12), .a21(matrix_multiplier_1_c21),
    .a22(matrix_multiplier_1_c22), .ini_11(32'h1), .ini_12(32'h1), .ini_21(32'h1), .ini_22({32{1'b0}}),
    .Enable(not_1_out), .CLK(clock_1_out), .out_11(n2_by_2_matrix_1_out_11),
    .out_12(n2_by_2_matrix_1_out_12), .out_13(n2_by_2_matrix_1_out_13), .out_14(n2_by_2_matrix_1_out_14));
  _2_by_2_matrix u_2_by_2_matrix_2 (
    .a11(matrix_multiplier_2_c11), .a12(matrix_multiplier_2_c12), .a21(matrix_multiplier_2_c21),
    .a22(matrix_multiplier_2_c22), .ini_11(32'h1), .ini_12({32{1'b0}}), .ini_21({32{1'b0}}), .ini_22(32'h1),
    .Enable(bit_extender_1_out), .CLK(clock_1_out), .out_11(n2_by_2_matrix_2_out_11),
    .out_12(n2_by_2_matrix_2_out_12), .out_13(n2_by_2_matrix_2_out_13), .out_14(n2_by_2_matrix_2_out_14));
  // Probe on n2_by_2_matrix_2_out_11
  // Probe on n2_by_2_matrix_2_out_13
  matrix_multiplier matrix_multiplier_1 (
    .a11(n2_by_2_matrix_1_out_11), .a12(n2_by_2_matrix_1_out_12), .a21(n2_by_2_matrix_1_out_13),
    .a22(n2_by_2_matrix_1_out_14), .in_5(n2_by_2_matrix_1_out_11), .in_6(n2_by_2_matrix_1_out_12),
    .in_7(n2_by_2_matrix_1_out_13), .in_8(n2_by_2_matrix_1_out_14), .c11(matrix_multiplier_1_c11),
    .c12(matrix_multiplier_1_c12), .c21(matrix_multiplier_1_c21), .c22(matrix_multiplier_1_c22));
  matrix_multiplier matrix_multiplier_2 (
    .a11(n2_by_2_matrix_1_out_11), .a12(n2_by_2_matrix_1_out_12), .a21(n2_by_2_matrix_1_out_13),
    .a22(n2_by_2_matrix_1_out_14), .in_5(n2_by_2_matrix_2_out_11), .in_6(n2_by_2_matrix_2_out_12),
    .in_7(n2_by_2_matrix_2_out_13), .in_8(n2_by_2_matrix_2_out_14), .c11(matrix_multiplier_2_c11),
    .c12(matrix_multiplier_2_c12), .c21(matrix_multiplier_2_c21), .c22(matrix_multiplier_2_c22));
  // Probe on n2_by_2_matrix_2_out_12
  // Probe on n2_by_2_matrix_2_out_14
  Multiplexer #(.width(32), .enable("false")) multiplexer_1 (
    .in0(n2_by_2_matrix_2_out_12), .in1({32{1'b0}}), .out(out_2), .sel(not_1_out));
endmodule

module matrix_multiplier (
  input  [31:0] a11,
  input  [31:0] a12,
  input  [31:0] a21,
  input  [31:0] a22,
  input  [31:0] in_5,
  input  [31:0] in_6,
  input  [31:0] in_7,
  input  [31:0] in_8,
  output [31:0] c11,
  output [31:0] c12,
  output [31:0] c21,
  output [31:0] c22
);

  wire [31:0] multiplier_1_out, multiplier_2_out, multiplier_3_out, multiplier_4_out, multiplier_5_out,
       multiplier_6_out, multiplier_7_out, multiplier_8_out;

  Multiplier #(.width(32)) multiplier_1 (.a(a11), .b(in_5), .out(multiplier_1_out));  // open: cin, cout
  Multiplier #(.width(32)) multiplier_2 (.a(a12), .b(in_7), .out(multiplier_2_out));  // open: cin, cout
  Multiplier #(.width(32)) multiplier_3 (.a(a11), .b(in_6), .out(multiplier_3_out));  // open: cin, cout
  Multiplier #(.width(32)) multiplier_4 (.a(a12), .b(in_8), .out(multiplier_4_out));  // open: cin, cout
  Multiplier #(.width(32)) multiplier_5 (.a(a21), .b(in_5), .out(multiplier_5_out));  // open: cin, cout
  Multiplier #(.width(32)) multiplier_6 (.a(a22), .b(in_7), .out(multiplier_6_out));  // open: cin, cout
  Multiplier #(.width(32)) multiplier_7 (.a(a21), .b(in_6), .out(multiplier_7_out));  // open: cin, cout
  Multiplier #(.width(32)) multiplier_8 (.a(a22), .b(in_8), .out(multiplier_8_out));  // open: cin, cout
  Adder #(.width(32)) adder_1 (.a(multiplier_1_out), .b(multiplier_2_out), .out(c11));  // open: cin, cout
  Adder #(.width(32)) adder_2 (.a(multiplier_3_out), .b(multiplier_4_out), .out(c12));  // open: cin, cout
  Adder #(.width(32)) adder_3 (.a(multiplier_5_out), .b(multiplier_6_out), .out(c21));  // open: cin, cout
  Adder #(.width(32)) adder_4 (.a(multiplier_7_out), .b(multiplier_8_out), .out(c22));  // open: cin, cout

  // Other names for the same wires on the sheet: b11[31:0] = in_5; b12[31:0] = in_6; b21[31:0] = in_7;
  //   b22[31:0] = in_8
endmodule

module _2_by_2_matrix (
  input  [31:0] ini_11,
  input  [31:0] ini_12,
  input  [31:0] ini_21,
  input  [31:0] ini_22,
  input  [31:0] a11,
  input  [31:0] a12,
  input  [31:0] a21,
  input  [31:0] a22,
  input  CLK,
  input  Enable,
  output [31:0] out_11,
  output [31:0] out_12,
  output [31:0] out_13,
  output [31:0] out_14
);

  initialized_register initialized_register_1 (.ini(ini_11), .Data(a11), .Enable(Enable), .CLK(CLK), .Q(out_11));
  initialized_register initialized_register_2 (.ini(ini_12), .Data(a12), .Enable(Enable), .CLK(CLK), .Q(out_12));
  initialized_register initialized_register_3 (.ini(ini_21), .Data(a21), .Enable(Enable), .CLK(CLK), .Q(out_13));
  initialized_register initialized_register_4 (.ini(ini_22), .Data(a22), .Enable(Enable), .CLK(CLK), .Q(out_14));
endmodule

module initialized_register (
  input  [31:0] ini,
  input  [31:0] Data,
  input  Enable,
  input  CLK,
  output [31:0] Q
);

  wire clock_1_out, comparator_1_eq, multiplexer_2_out;
  wire [1:0] counter_1_q;
  wire [31:0] multiplexer_1_out;

  Clock clock_1 (.out(clock_1_out));
  Counter #(.width(2), .max('h3), .ongoal("stay")) counter_1 (
    .Q(counter_1_q), .clk(clock_1_out));  // open: load, D, count, carry, clr
  Multiplexer #(.width(32), .enable("false")) multiplexer_1 (
    .in0(Data), .in1(ini), .out(multiplexer_1_out), .sel(comparator_1_eq));
  Multiplexer #(.enable("false")) multiplexer_2 (
    .in0(Enable), .in1(1'b1), .out(multiplexer_2_out), .sel(comparator_1_eq));
  Comparator #(.width(2), .mode("unsigned")) comparator_1 (
    .a(counter_1_q), .b(2'b01), .eq(comparator_1_eq));  // open: gt, lt
  Register #(.width(32)) register_1 (.D(multiplexer_1_out), .en(multiplexer_2_out), .Q(Q), .clk(CLK));  // open: clr
endmodule
