// Logisim project 瞎搞.circ as structural Verilog: 3 circuits, main circuit main
module main (
  input  Reset,
  input  Set,
  output Q,
  output nQ
);

  wire d_latch_1_out_2;

  nor nor_1 (Q, Reset, nQ);
  nor nor_2 (nQ, Q, Set);
  D_Latch d_latch_1 (.D(d_latch_1_out_2), .out_2(d_latch_1_out_2), .out_3(d_latch_1_out_2));
endmodule

module D_Latch (
  input  D,
  output out_2,
  output out_3
);

  wire CLK_out;

  Clock CLK (.out(CLK_out));
  buf and_1 (out_2, CLK_out);  // AND_Gate AND_Gate
  buf and_2 (out_3, D);  // AND_Gate
endmodule

module D_Trigger (
);

  D_Latch d_latch_1 ();  // open: D, out_2, out_3
endmodule
